// Logisim project CircuitoDivisorVersãoFinal2.circ as structural Verilog: 3 circuits, main circuit Subtrator8bits
module main (
  input  [31:0] in_1,
  input  [31:0] in_2,
  input  Bit_Enable,
  output [31:0] out_4,
  output [31:0] out_5
);

  wire enabler_1_out_18, enabler_1_out_19, enabler_1_out_20, enabler_1_out_21, enabler_1_out_22,
       enabler_1_out_23, enabler_1_out_24, enabler_1_out_25, enabler_1_out_26, enabler_1_out_27,
       enabler_1_out_28, enabler_1_out_29, enabler_1_out_30, enabler_1_out_31, enabler_1_out_32,
       enabler_1_out_33, subtrator8bits_1_out_17, subtrator8bits_1_out_25, subtrator8bits_2_out_17,
       subtrator8bits_2_out_24, subtrator8bits_2_out_25, subtrator8bits_3_out_17, subtrator8bits_3_out_23,
       subtrator8bits_3_out_24, subtrator8bits_3_out_25, subtrator8bits_4_out_17, subtrator8bits_4_out_22,
       subtrator8bits_4_out_23, subtrator8bits_4_out_24, subtrator8bits_4_out_25, subtrator8bits_5_out_17,
       subtrator8bits_5_out_21, subtrator8bits_5_out_22, subtrator8bits_5_out_23, subtrator8bits_5_out_24,
       subtrator8bits_5_out_25, subtrator8bits_6_out_17, subtrator8bits_6_out_20, subtrator8bits_6_out_21,
       subtrator8bits_6_out_22, subtrator8bits_6_out_23, subtrator8bits_6_out_24, subtrator8bits_6_out_25,
       subtrator8bits_7_out_17, subtrator8bits_7_out_19, subtrator8bits_7_out_20, subtrator8bits_7_out_21,
       subtrator8bits_7_out_22, subtrator8bits_7_out_23, subtrator8bits_7_out_24, subtrator8bits_7_out_25,
       subtrator8bits_8_out_17;
  wire [7:0] bit_extender_1_out, bit_extender_2_out, not_8_out, subtrator8bits_8_out_25;

  Bit_Extender #(.in_width(32), .out_width(8)) bit_extender_1 (.in(in_1), .out(bit_extender_1_out));
  Bit_Extender #(.in_width(32), .out_width(8)) bit_extender_2 (.in(in_2), .out(bit_extender_2_out));
  Enabler enabler_1 (
    .in_17(Bit_Enable), .in_1(bit_extender_1_out[7]), .in_2(bit_extender_1_out[6]),
    .in_3(bit_extender_1_out[5]), .in_4(bit_extender_1_out[4]), .in_5(bit_extender_1_out[3]),
    .in_6(bit_extender_1_out[2]), .in_7(bit_extender_1_out[1]), .in_8(bit_extender_1_out[0]),
    .in_9(bit_extender_2_out[7]), .in_10(bit_extender_2_out[6]), .in_11(bit_extender_2_out[5]),
    .in_12(bit_extender_2_out[4]), .in_13(bit_extender_2_out[3]), .in_14(bit_extender_2_out[2]),
    .in_15(bit_extender_2_out[1]), .in_16(bit_extender_2_out[0]), .out_18(enabler_1_out_18),
    .out_19(enabler_1_out_19), .out_20(enabler_1_out_20), .out_21(enabler_1_out_21),
    .out_22(enabler_1_out_22), .out_23(enabler_1_out_23), .out_24(enabler_1_out_24),
    .out_25(enabler_1_out_25), .out_26(enabler_1_out_26), .out_27(enabler_1_out_27),
    .out_28(enabler_1_out_28), .out_29(enabler_1_out_29), .out_30(enabler_1_out_30),
    .out_31(enabler_1_out_31), .out_32(enabler_1_out_32), .out_33(enabler_1_out_33));
  Subtrator8bits subtrator8bits_1 (
    .in_1(1'b0), .in_2(1'b0), .in_3(1'b0), .in_4(1'b0), .in_5(1'b0), .in_6(1'b0), .in_7(1'b0),
    .in_8(enabler_1_out_18), .in_9(enabler_1_out_26), .in_10(enabler_1_out_27), .in_11(enabler_1_out_28),
    .in_12(enabler_1_out_29), .in_13(enabler_1_out_30), .in_14(enabler_1_out_31), .in_15(enabler_1_out_32),
    .in_16(enabler_1_out_33), .out_25(subtrator8bits_1_out_25), .out_17(subtrator8bits_1_out_17));  // open: out_18, out_19, out_20, out_21, out_22, out_23, out_24
  Subtrator8bits subtrator8bits_2 (
    .in_1(1'b0), .in_2(1'b0), .in_3(1'b0), .in_4(1'b0), .in_5(1'b0), .in_6(1'b0),
    .in_7(subtrator8bits_1_out_25), .in_8(enabler_1_out_19), .in_9(enabler_1_out_26),
    .in_10(enabler_1_out_27), .in_11(enabler_1_out_28), .in_12(enabler_1_out_29), .in_13(enabler_1_out_30),
    .in_14(enabler_1_out_31), .in_15(enabler_1_out_32), .in_16(enabler_1_out_33),
    .out_24(subtrator8bits_2_out_24), .out_25(subtrator8bits_2_out_25), .out_17(subtrator8bits_2_out_17));  // open: out_18, out_19, out_20, out_21, out_22, out_23
  Subtrator8bits subtrator8bits_3 (
    .in_1(1'b0), .in_2(1'b0), .in_3(1'b0), .in_4(1'b0), .in_5(1'b0), .in_6(subtrator8bits_2_out_24),
    .in_7(subtrator8bits_2_out_25), .in_8(enabler_1_out_20), .in_9(enabler_1_out_26),
    .in_10(enabler_1_out_27), .in_11(enabler_1_out_28), .in_12(enabler_1_out_29), .in_13(enabler_1_out_30),
    .in_14(enabler_1_out_31), .in_15(enabler_1_out_32), .in_16(enabler_1_out_33),
    .out_23(subtrator8bits_3_out_23), .out_24(subtrator8bits_3_out_24), .out_25(subtrator8bits_3_out_25),
    .out_17(subtrator8bits_3_out_17));  // open: out_18, out_19, out_20, out_21, out_22
  Subtrator8bits subtrator8bits_4 (
    .in_1(1'b0), .in_2(1'b0), .in_3(1'b0), .in_4(1'b0), .in_5(subtrator8bits_3_out_23),
    .in_6(subtrator8bits_3_out_24), .in_7(subtrator8bits_3_out_25), .in_8(enabler_1_out_21),
    .in_9(enabler_1_out_26), .in_10(enabler_1_out_27), .in_11(enabler_1_out_28), .in_12(enabler_1_out_29),
    .in_13(enabler_1_out_30), .in_14(enabler_1_out_31), .in_15(enabler_1_out_32), .in_16(enabler_1_out_33),
    .out_22(subtrator8bits_4_out_22), .out_23(subtrator8bits_4_out_23), .out_24(subtrator8bits_4_out_24),
    .out_25(subtrator8bits_4_out_25), .out_17(subtrator8bits_4_out_17));  // open: out_18, out_19, out_20, out_21
  Subtrator8bits subtrator8bits_5 (
    .in_1(1'b0), .in_2(1'b0), .in_3(1'b0), .in_4(subtrator8bits_4_out_22), .in_5(subtrator8bits_4_out_23),
    .in_6(subtrator8bits_4_out_24), .in_7(subtrator8bits_4_out_25), .in_8(enabler_1_out_22),
    .in_9(enabler_1_out_26), .in_10(enabler_1_out_27), .in_11(enabler_1_out_28), .in_12(enabler_1_out_29),
    .in_13(enabler_1_out_30), .in_14(enabler_1_out_31), .in_15(enabler_1_out_32), .in_16(enabler_1_out_33),
    .out_21(subtrator8bits_5_out_21), .out_22(subtrator8bits_5_out_22), .out_23(subtrator8bits_5_out_23),
    .out_24(subtrator8bits_5_out_24), .out_25(subtrator8bits_5_out_25), .out_17(subtrator8bits_5_out_17));  // open: out_18, out_19, out_20
  Subtrator8bits subtrator8bits_6 (
    .in_1(1'b0), .in_2(1'b0), .in_3(subtrator8bits_5_out_21), .in_4(subtrator8bits_5_out_22),
    .in_5(subtrator8bits_5_out_23), .in_6(subtrator8bits_5_out_24), .in_7(subtrator8bits_5_out_25),
    .in_8(enabler_1_out_23), .in_9(enabler_1_out_26), .in_10(enabler_1_out_27), .in_11(enabler_1_out_28),
    .in_12(enabler_1_out_29), .in_13(enabler_1_out_30), .in_14(enabler_1_out_31), .in_15(enabler_1_out_32),
    .in_16(enabler_1_out_33), .out_20(subtrator8bits_6_out_20), .out_21(subtrator8bits_6_out_21),
    .out_22(subtrator8bits_6_out_22), .out_23(subtrator8bits_6_out_23), .out_24(subtrator8bits_6_out_24),
    .out_25(subtrator8bits_6_out_25), .out_17(subtrator8bits_6_out_17));  // open: out_18, out_19
  Subtrator8bits subtrator8bits_7 (
    .in_1(1'b0), .in_2(subtrator8bits_6_out_20), .in_3(subtrator8bits_6_out_21),
    .in_4(subtrator8bits_6_out_22), .in_5(subtrator8bits_6_out_23), .in_6(subtrator8bits_6_out_24),
    .in_7(subtrator8bits_6_out_25), .in_8(enabler_1_out_24), .in_9(enabler_1_out_26),
    .in_10(enabler_1_out_27), .in_11(enabler_1_out_28), .in_12(enabler_1_out_29), .in_13(enabler_1_out_30),
    .in_14(enabler_1_out_31), .in_15(enabler_1_out_32), .in_16(enabler_1_out_33),
    .out_19(subtrator8bits_7_out_19), .out_20(subtrator8bits_7_out_20), .out_21(subtrator8bits_7_out_21),
    .out_22(subtrator8bits_7_out_22), .out_23(subtrator8bits_7_out_23), .out_24(subtrator8bits_7_out_24),
    .out_25(subtrator8bits_7_out_25), .out_17(subtrator8bits_7_out_17));  // open: out_18
  Subtrator8bits subtrator8bits_8 (
    .in_1(subtrator8bits_7_out_19), .in_2(subtrator8bits_7_out_20), .in_3(subtrator8bits_7_out_21),
    .in_4(subtrator8bits_7_out_22), .in_5(subtrator8bits_7_out_23), .in_6(subtrator8bits_7_out_24),
    .in_7(subtrator8bits_7_out_25), .in_8(enabler_1_out_25), .in_9(enabler_1_out_26),
    .in_10(enabler_1_out_27), .in_11(enabler_1_out_28), .in_12(enabler_1_out_29), .in_13(enabler_1_out_30),
    .in_14(enabler_1_out_31), .in_15(enabler_1_out_32), .in_16(enabler_1_out_33),
    .out_18(subtrator8bits_8_out_25[7]), .out_19(subtrator8bits_8_out_25[6]),
    .out_20(subtrator8bits_8_out_25[5]), .out_21(subtrator8bits_8_out_25[4]),
    .out_22(subtrator8bits_8_out_25[3]), .out_23(subtrator8bits_8_out_25[2]),
    .out_24(subtrator8bits_8_out_25[1]), .out_25(subtrator8bits_8_out_25[0]), .out_17(subtrator8bits_8_out_17));
  not not_1 (not_8_out[7], subtrator8bits_1_out_17);
  not not_2 (not_8_out[5], subtrator8bits_3_out_17);
  not not_3 (not_8_out[4], subtrator8bits_4_out_17);
  not not_4 (not_8_out[6], subtrator8bits_2_out_17);
  not not_5 (not_8_out[3], subtrator8bits_5_out_17);
  not not_6 (not_8_out[2], subtrator8bits_6_out_17);
  not not_7 (not_8_out[1], subtrator8bits_7_out_17);
  not not_8 (not_8_out[0], subtrator8bits_8_out_17);
  assign out_4 = {{24{1'b0}}, not_8_out};  // Bit_Extender bit_extender_3
  assign out_5 = {{24{1'b0}}, subtrator8bits_8_out_25};  // Bit_Extender bit_extender_4

  // Notes on the sheet:
  //   Dividendo
  //   Divisor
  //   Enabler
endmodule

// Subtrator Modificado
module Subtrator8bits (
  input  in_1,
  input  in_2,
  input  in_3,
  input  in_4,
  input  in_5,
  input  in_6,
  input  in_7,
  input  in_8,
  input  in_9,
  input  in_10,
  input  in_11,
  input  in_12,
  input  in_13,
  input  in_14,
  input  in_15,
  input  in_16,
  output out_17,
  output out_18,
  output out_19,
  output out_20,
  output out_21,
  output out_22,
  output out_23,
  output out_24,
  output out_25
);

  wire and_1_out, and_2_out, and_3_out, and_4_out, and_5_out, and_6_out, and_7_out, and_8_out, and_9_out,
       and_10_out, and_11_out, and_12_out, and_13_out, and_14_out, and_15_out, and_16_out, and_17_out,
       and_18_out, and_19_out, and_20_out, and_21_out, and_22_out, and_23_out, and_24_out, and_25_out,
       and_26_out, and_27_out, and_28_out, and_29_out, and_30_out, and_31_out, and_32_out, and_33_out,
       and_34_out, and_35_out, and_36_out, and_37_out, and_38_out, and_39_out, and_40_out, not_1_out,
       not_2_out, not_3_out, not_4_out, not_5_out, not_6_out, not_7_out, not_8_out, or_3_out, or_8_out,
       or_11_out, or_12_out, or_13_out, or_14_out, or_15_out, xor_1_out, xor_2_out, xor_3_out, xor_4_out,
       xor_5_out, xor_6_out, xor_7_out, xor_8_out, xor_9_out, xor_10_out, xor_11_out, xor_12_out, xor_13_out,
       xor_14_out, xor_15_out, xor_16_out;

  and and_1 (and_1_out, in_1, out_17);
  not not_1 (not_1_out, in_8);
  and and_2 (and_2_out, xor_16_out, ~out_17);  // AND_Gate
  and and_3 (and_3_out, in_3, out_17);
  or or_1 (out_18, and_1_out, and_2_out);
  xor xor_1 (xor_1_out, in_8, in_16);
  and and_4 (and_4_out, not_1_out, in_16);
  and and_5 (and_5_out, not_1_out, 1'b0);
  and and_6 (and_6_out, in_16, 1'b0);
  and and_7 (and_7_out, xor_12_out, ~out_17);  // AND_Gate
  and and_8 (and_8_out, in_2, out_17);
  or or_2 (out_20, and_3_out, and_7_out);
  xor xor_2 (xor_2_out, xor_1_out, 1'b0);
  or or_3 (or_3_out, and_4_out, and_5_out, and_6_out);
  and and_9 (and_9_out, in_4, out_17);
  and and_10 (and_10_out, xor_14_out, ~out_17);  // AND_Gate
  or or_4 (out_19, and_8_out, and_10_out);
  not not_2 (not_2_out, in_7);
  and and_11 (and_11_out, xor_10_out, ~out_17);  // AND_Gate
  and and_12 (and_12_out, in_5, out_17);
  or or_5 (out_21, and_9_out, and_11_out);
  xor xor_3 (xor_3_out, in_7, in_15);
  and and_13 (and_13_out, not_2_out, in_15);
  and and_14 (and_14_out, not_2_out, or_3_out);
  and and_15 (and_15_out, in_15, or_3_out);
  and and_16 (and_16_out, in_6, out_17);
  and and_17 (and_17_out, xor_8_out, ~out_17);  // AND_Gate
  or or_6 (out_22, and_12_out, and_17_out);
  and and_18 (and_18_out, in_7, out_17);
  and and_19 (and_19_out, xor_6_out, ~out_17);  // AND_Gate
  or or_7 (out_23, and_16_out, and_19_out);
  xor xor_4 (xor_4_out, xor_3_out, or_3_out);
  or or_8 (or_8_out, and_13_out, and_14_out, and_15_out);
  and and_20 (and_20_out, in_8, out_17);
  and and_21 (and_21_out, xor_4_out, ~out_17);  // AND_Gate
  or or_9 (out_24, and_18_out, and_21_out);
  xor xor_5 (xor_5_out, in_6, in_14);
  not not_3 (not_3_out, in_6);
  and and_22 (and_22_out, not_3_out, in_14);
  and and_23 (and_23_out, not_3_out, or_8_out);
  and and_24 (and_24_out, in_14, or_8_out);
  and and_25 (and_25_out, xor_2_out, ~out_17);  // AND_Gate
  or or_10 (out_25, and_20_out, and_25_out);
  xor xor_6 (xor_6_out, xor_5_out, or_8_out);
  or or_11 (or_11_out, and_22_out, and_23_out, and_24_out);
  xor xor_7 (xor_7_out, in_5, in_13);
  not not_4 (not_4_out, in_5);
  and and_26 (and_26_out, not_4_out, in_13);
  and and_27 (and_27_out, not_4_out, or_11_out);
  and and_28 (and_28_out, in_13, or_11_out);
  xor xor_8 (xor_8_out, xor_7_out, or_11_out);
  or or_12 (or_12_out, and_26_out, and_27_out, and_28_out);
  not not_5 (not_5_out, in_4);
  and and_29 (and_29_out, not_5_out, in_12);
  and and_30 (and_30_out, not_5_out, or_12_out);
  and and_31 (and_31_out, in_12, or_12_out);
  xor xor_9 (xor_9_out, in_4, in_12);
  xor xor_10 (xor_10_out, xor_9_out, or_12_out);
  or or_13 (or_13_out, and_29_out, and_30_out, and_31_out);
  not not_6 (not_6_out, in_3);
  xor xor_11 (xor_11_out, in_3, in_11);
  and and_32 (and_32_out, not_6_out, in_11);
  and and_33 (and_33_out, not_6_out, or_13_out);
  and and_34 (and_34_out, in_11, or_13_out);
  xor xor_12 (xor_12_out, xor_11_out, or_13_out);
  or or_14 (or_14_out, and_32_out, and_33_out, and_34_out);
  not not_7 (not_7_out, in_2);
  xor xor_13 (xor_13_out, in_2, in_10);
  and and_35 (and_35_out, not_7_out, in_10);
  and and_36 (and_36_out, not_7_out, or_14_out);
  and and_37 (and_37_out, in_10, or_14_out);
  xor xor_14 (xor_14_out, xor_13_out, or_14_out);
  or or_15 (or_15_out, and_35_out, and_36_out, and_37_out);
  not not_8 (not_8_out, in_1);
  xor xor_15 (xor_15_out, in_1, in_9);
  and and_38 (and_38_out, not_8_out, in_9);
  and and_39 (and_39_out, not_8_out, or_15_out);
  and and_40 (and_40_out, in_9, or_15_out);
  xor xor_16 (xor_16_out, xor_15_out, or_15_out);
  or or_16 (out_17, and_38_out, and_39_out, and_40_out);
endmodule

module Enabler (
  input  in_1,
  input  in_2,
  input  in_3,
  input  in_4,
  input  in_5,
  input  in_6,
  input  in_7,
  input  in_8,
  input  in_9,
  input  in_10,
  input  in_11,
  input  in_12,
  input  in_13,
  input  in_14,
  input  in_15,
  input  in_16,
  input  in_17,
  output out_18,
  output out_19,
  output out_20,
  output out_21,
  output out_22,
  output out_23,
  output out_24,
  output out_25,
  output out_26,
  output out_27,
  output out_28,
  output out_29,
  output out_30,
  output out_31,
  output out_32,
  output out_33
);

  and and_1 (out_18, in_17, in_1);
  and and_2 (out_19, in_17, in_2);
  and and_3 (out_20, in_17, in_3);
  and and_4 (out_22, in_17, in_5);
  and and_5 (out_21, in_17, in_4);
  and and_6 (out_24, in_17, in_7);
  and and_7 (out_23, in_17, in_6);
  and and_8 (out_25, in_17, in_8);
  and and_9 (out_26, in_17, in_9);
  and and_10 (out_27, in_17, in_10);
  and and_11 (out_28, in_17, in_11);
  and and_12 (out_29, in_17, in_12);
  and and_13 (out_30, in_17, in_13);
  and and_14 (out_31, in_17, in_14);
  and and_15 (out_32, in_17, in_15);
  and and_16 (out_33, in_17, in_16);
endmodule
