// Logisim project Multiplicador 32bits.circ as structural Verilog: 3 circuits, main circuit somador 2bits
module MULTIPLICADOR_32_BITS (
  input  [31:0] in_1,
  input  [31:0] in_2,
  input  in_3,
  output [31:0] out_4
);

  wire adder_1_cout, adder_1_out, adder_2_cout, adder_2_out, adder_3_cout, adder_3_out, adder_4_cout,
       adder_4_out, adder_5_cout, adder_5_out, adder_6_cout, adder_6_out, adder_7_cout, adder_7_out,
       adder_8_cout, adder_8_out, adder_9_cout, adder_9_out, adder_10_cout, adder_10_out, adder_11_cout,
       adder_11_out, adder_12_cout, adder_12_out, adder_13_cout, adder_13_out, adder_14_cout, adder_14_out,
       adder_15_cout, adder_15_out, adder_16_cout, adder_16_out, adder_17_cout, adder_17_out, adder_18_cout,
       adder_18_out, adder_19_cout, adder_19_out, adder_20_cout, adder_20_out, adder_21_cout, adder_21_out,
       adder_22_cout, adder_22_out, adder_23_cout, adder_23_out, adder_24_cout, adder_24_out, adder_25_cout,
       adder_25_out, adder_26_cout, adder_26_out, adder_27_cout, adder_27_out, adder_28_cout, adder_28_out,
       adder_29_cout, adder_29_out, adder_30_cout, adder_30_out, adder_31_cout, adder_31_out, adder_32_cout,
       adder_32_out, adder_33_cout, adder_33_out, adder_34_cout, adder_34_out, adder_35_cout, adder_35_out,
       adder_36_cout, adder_36_out, adder_37_cout, adder_37_out, adder_38_cout, adder_38_out, adder_39_cout,
       adder_39_out, adder_40_cout, adder_40_out, adder_41_cout, adder_41_out, adder_42_cout, adder_42_out,
       adder_43_cout, adder_43_out, adder_44_cout, adder_44_out, adder_45_cout, adder_45_out, adder_46_cout,
       adder_46_out, adder_47_cout, adder_47_out, adder_48_cout, adder_48_out, adder_49_cout, adder_49_out,
       adder_50_cout, adder_50_out, adder_51_cout, adder_51_out, adder_52_cout, adder_52_out, adder_53_cout,
       adder_53_out, adder_54_cout, adder_54_out, adder_55_cout, adder_55_out, adder_56_cout, adder_56_out,
       adder_57_cout, adder_57_out, adder_58_cout, adder_58_out, adder_59_cout, adder_59_out, adder_60_cout,
       adder_60_out, adder_61_cout, adder_61_out, adder_62_cout, adder_62_out, adder_63_cout, adder_63_out,
       adder_64_cout, adder_64_out, adder_65_cout, adder_65_out, adder_66_cout, adder_66_out, adder_67_cout,
       adder_67_out, adder_68_cout, adder_68_out, adder_69_cout, adder_69_out, adder_70_cout, adder_70_out,
       adder_71_cout, adder_71_out, adder_72_cout, adder_72_out, adder_73_cout, adder_73_out, adder_74_cout,
       adder_74_out, adder_75_cout, adder_75_out, adder_76_cout, adder_76_out, adder_77_cout, adder_77_out,
       adder_78_cout, adder_78_out, adder_79_cout, adder_79_out, adder_80_cout, adder_80_out, adder_81_cout,
       adder_81_out, adder_82_cout, adder_82_out, adder_83_cout, adder_83_out, adder_84_cout, adder_84_out,
       adder_85_cout, adder_85_out, adder_86_cout, adder_86_out, adder_87_cout, adder_87_out, adder_88_cout,
       adder_88_out, adder_89_cout, adder_89_out, adder_90_cout, adder_90_out, adder_91_cout, adder_91_out,
       adder_92_cout, adder_92_out, adder_93_cout, adder_93_out, adder_94_cout, adder_94_out, adder_95_cout,
       adder_95_out, adder_96_cout, adder_96_out, adder_97_cout, adder_97_out, adder_98_cout, adder_98_out,
       adder_99_cout, adder_99_out, adder_100_cout, adder_100_out, adder_101_cout, adder_101_out,
       adder_102_cout, adder_102_out, adder_103_cout, adder_103_out, adder_104_cout, adder_104_out,
       adder_105_cout, adder_105_out, adder_106_cout, adder_106_out, adder_107_cout, adder_107_out,
       adder_108_cout, adder_108_out, adder_109_cout, adder_109_out, adder_110_cout, adder_110_out,
       adder_111_cout, adder_111_out, adder_112_cout, adder_112_out, adder_113_cout, adder_113_out,
       adder_114_cout, adder_114_out, adder_115_cout, adder_115_out, adder_116_cout, adder_116_out,
       adder_117_cout, adder_117_out, adder_118_cout, adder_118_out, adder_119_cout, adder_119_out,
       adder_120_cout, adder_120_out, adder_121_cout, adder_121_out, adder_122_cout, adder_122_out,
       adder_123_cout, adder_123_out, adder_124_cout, adder_124_out, adder_125_cout, adder_125_out,
       adder_126_cout, adder_126_out, adder_127_cout, adder_127_out, adder_128_cout, adder_128_out,
       adder_129_cout, adder_129_out, adder_130_cout, adder_130_out, adder_131_cout, adder_131_out,
       adder_132_cout, adder_132_out, adder_133_cout, adder_133_out, adder_134_cout, adder_134_out,
       adder_135_cout, adder_135_out, adder_136_cout, adder_136_out, adder_137_cout, adder_137_out,
       adder_138_cout, adder_138_out, adder_139_cout, adder_139_out, adder_140_cout, adder_140_out,
       adder_141_cout, adder_141_out, adder_142_cout, adder_142_out, adder_143_cout, adder_143_out,
       adder_144_cout, adder_144_out, adder_145_cout, adder_145_out, adder_146_cout, adder_146_out,
       adder_147_cout, adder_147_out, adder_148_cout, adder_148_out, adder_149_cout, adder_149_out,
       adder_150_cout, adder_150_out, adder_151_cout, adder_151_out, adder_152_cout, adder_152_out,
       adder_153_cout, adder_153_out, adder_154_cout, adder_154_out, adder_155_cout, adder_155_out,
       adder_156_cout, adder_156_out, adder_157_cout, adder_157_out, adder_158_cout, adder_158_out,
       adder_159_cout, adder_159_out, adder_160_cout, adder_160_out, adder_161_cout, adder_161_out,
       adder_162_cout, adder_162_out, adder_163_cout, adder_163_out, adder_164_cout, adder_164_out,
       adder_165_cout, adder_165_out, adder_166_cout, adder_166_out, adder_167_cout, adder_167_out,
       adder_168_cout, adder_168_out, adder_169_cout, adder_169_out, adder_170_cout, adder_170_out,
       adder_171_cout, adder_171_out, adder_172_cout, adder_172_out, adder_173_cout, adder_173_out,
       adder_174_cout, adder_174_out, adder_175_cout, adder_175_out, adder_176_cout, adder_176_out,
       adder_177_cout, adder_177_out, adder_178_cout, adder_178_out, adder_179_cout, adder_179_out,
       adder_180_cout, adder_180_out, adder_181_cout, adder_181_out, adder_182_cout, adder_182_out,
       adder_183_cout, adder_183_out, adder_184_cout, adder_184_out, adder_185_cout, adder_185_out,
       adder_186_cout, adder_186_out, adder_187_cout, adder_187_out, adder_188_cout, adder_188_out,
       adder_189_cout, adder_189_out, adder_190_cout, adder_190_out, adder_191_cout, adder_191_out,
       adder_192_cout, adder_192_out, adder_193_cout, adder_193_out, adder_194_cout, adder_194_out,
       adder_195_cout, adder_195_out, adder_196_cout, adder_196_out, adder_197_cout, adder_197_out,
       adder_198_cout, adder_198_out, adder_199_cout, adder_199_out, adder_200_cout, adder_200_out,
       adder_201_cout, adder_201_out, adder_202_cout, adder_202_out, adder_203_cout, adder_203_out,
       adder_204_cout, adder_204_out, adder_205_cout, adder_205_out, adder_206_cout, adder_206_out,
       adder_207_cout, adder_207_out, adder_208_cout, adder_208_out, adder_209_cout, adder_209_out,
       adder_210_cout, adder_210_out, adder_211_cout, adder_211_out, adder_212_cout, adder_212_out,
       adder_213_cout, adder_213_out, adder_214_cout, adder_214_out, adder_215_cout, adder_215_out,
       adder_216_cout, adder_216_out, adder_217_cout, adder_217_out, adder_218_cout, adder_218_out,
       adder_219_cout, adder_219_out, adder_220_cout, adder_220_out, adder_221_cout, adder_221_out,
       adder_222_cout, adder_222_out, adder_223_cout, adder_223_out, adder_224_cout, adder_224_out,
       and_1_out, and_3_out, and_4_out, and_6_out, and_7_out, and_8_out, and_9_out, and_11_out, and_12_out,
       and_13_out, and_14_out, and_16_out, and_17_out, and_18_out, and_19_out, and_20_out, and_22_out,
       and_23_out, and_24_out, and_25_out, and_26_out, and_28_out, and_29_out, and_30_out, and_31_out,
       and_32_out, and_33_out, and_34_out, and_36_out, and_37_out, and_38_out, and_39_out, and_40_out,
       and_41_out, and_42_out, and_43_out, and_45_out, and_46_out, and_47_out, and_48_out, and_49_out,
       and_50_out, and_51_out, and_52_out, and_53_out, and_55_out, and_56_out, and_57_out, and_58_out,
       and_59_out, and_60_out, and_61_out, and_62_out, and_63_out, and_64_out, and_65_out, and_67_out,
       and_68_out, and_69_out, and_70_out, and_71_out, and_72_out, and_73_out, and_74_out, and_75_out,
       and_76_out, and_77_out, and_79_out, and_80_out, and_81_out, and_82_out, and_83_out, and_84_out,
       and_85_out, and_86_out, and_87_out, and_88_out, and_89_out, and_90_out, and_92_out, and_93_out,
       and_94_out, and_95_out, and_96_out, and_97_out, and_98_out, and_99_out, and_100_out, and_101_out,
       and_102_out, and_103_out, and_104_out, and_106_out, and_107_out, and_108_out, and_109_out,
       and_110_out, and_111_out, and_112_out, and_113_out, and_114_out, and_115_out, and_116_out,
       and_117_out, and_118_out, and_120_out, and_121_out, and_122_out, and_123_out, and_124_out,
       and_125_out, and_126_out, and_127_out, and_128_out, and_129_out, and_130_out, and_131_out,
       and_132_out, and_133_out, and_134_out, and_136_out, and_137_out, and_138_out, and_139_out,
       and_140_out, and_141_out, and_142_out, and_143_out, and_144_out, and_145_out, and_146_out,
       and_147_out, and_148_out, and_149_out, and_150_out, and_151_out, and_153_out, and_154_out,
       and_155_out, and_156_out, and_157_out, and_158_out, and_159_out, and_160_out, and_161_out,
       and_162_out, and_163_out, and_164_out, and_165_out, and_166_out, and_167_out, and_169_out,
       and_170_out, and_171_out, and_172_out, and_173_out, and_174_out, and_175_out, and_176_out,
       and_177_out, and_178_out, and_179_out, and_180_out, and_181_out, and_182_out, and_184_out,
       and_185_out, and_186_out, and_187_out, and_188_out, and_189_out, and_190_out, and_191_out,
       and_192_out, and_193_out, and_194_out, and_195_out, and_196_out, and_198_out, and_199_out,
       and_200_out, and_201_out, and_202_out, and_203_out, and_204_out, and_205_out, and_206_out,
       and_207_out, and_208_out, and_209_out, and_210_out, and_212_out, and_213_out, and_214_out,
       and_215_out, and_216_out, and_217_out, and_218_out, and_219_out, and_220_out, and_221_out,
       and_223_out, and_224_out, and_225_out, and_226_out, and_227_out, and_228_out, and_229_out,
       and_230_out, and_231_out, and_232_out, and_233_out, and_235_out, and_236_out, and_237_out,
       and_238_out, and_239_out, and_240_out, and_241_out, and_242_out, and_243_out, and_245_out,
       and_246_out, and_247_out, and_248_out, and_249_out, and_250_out, and_251_out, and_253_out,
       and_254_out, and_255_out, and_256_out, and_257_out, and_258_out, and_259_out, and_260_out,
       and_262_out, and_263_out, and_264_out, and_265_out, and_266_out, and_268_out, and_269_out,
       and_270_out, and_271_out, and_272_out, and_274_out, and_275_out, and_276_out, and_277_out,
       and_278_out, and_280_out, and_281_out, and_283_out, and_284_out, and_286_out,
       somador_2bits_1_resultado, somador_2bits_1_vai_1, somador_2bits_2_resultado, somador_2bits_2_vai_1;
  wire [15:0] bit_extender_1_out, bit_extender_2_out;

  Bit_Extender #(.in_width(32)) bit_extender_1 (.in(in_1), .out(bit_extender_1_out));
  Bit_Extender #(.in_width(32)) bit_extender_2 (.in(in_2), .out(bit_extender_2_out));
  and and_1 (and_1_out, bit_extender_1_out[0], bit_extender_2_out[0]);
  and and_2 (out_4[0], and_1_out, in_3);
  and and_3 (and_3_out, bit_extender_1_out[1], bit_extender_2_out[0]);
  and and_4 (and_4_out, bit_extender_1_out[0], bit_extender_2_out[1]);
  somador_2bits somador_2bits_1 (
    .A(and_4_out), .B(and_3_out), .RESULTADO(somador_2bits_1_resultado), .VAI_1(somador_2bits_1_vai_1));
  and and_5 (out_4[1], somador_2bits_1_resultado, in_3);
  and and_6 (and_6_out, bit_extender_1_out[2], bit_extender_2_out[0]);
  and and_7 (and_7_out, bit_extender_1_out[1], bit_extender_2_out[1]);
  and and_8 (and_8_out, bit_extender_1_out[0], bit_extender_2_out[2]);
  Adder #(.width(1)) adder_1 (
    .a(and_6_out), .b(somador_2bits_1_vai_1), .out(adder_1_out), .cin(and_7_out), .cout(adder_1_cout));
  and and_9 (and_9_out, bit_extender_1_out[3], bit_extender_2_out[0]);
  Adder #(.width(1)) adder_2 (
    .a(adder_1_out), .b(adder_1_cout), .out(adder_2_out), .cin(and_8_out), .cout(adder_2_cout));
  and and_10 (out_4[2], adder_2_out, in_3);
  and and_11 (and_11_out, bit_extender_1_out[2], bit_extender_2_out[1]);
  and and_12 (and_12_out, bit_extender_1_out[1], bit_extender_2_out[2]);
  and and_13 (and_13_out, bit_extender_1_out[0], bit_extender_2_out[3]);
  Adder #(.width(1)) adder_3 (
    .a(and_9_out), .b(adder_2_cout), .out(adder_3_out), .cin(and_11_out), .cout(adder_3_cout));
  Adder #(.width(1)) adder_4 (
    .a(adder_3_out), .b(adder_3_cout), .out(adder_4_out), .cin(and_12_out), .cout(adder_4_cout));
  Adder #(.width(1)) adder_5 (
    .a(adder_4_out), .b(adder_4_cout), .out(adder_5_out), .cin(and_13_out), .cout(adder_5_cout));
  and and_14 (and_14_out, bit_extender_1_out[4], bit_extender_2_out[0]);
  and and_15 (out_4[3], adder_5_out, in_3);
  and and_16 (and_16_out, bit_extender_1_out[3], bit_extender_2_out[1]);
  and and_17 (and_17_out, bit_extender_1_out[1], bit_extender_2_out[3]);
  and and_18 (and_18_out, bit_extender_1_out[2], bit_extender_2_out[2]);
  and and_19 (and_19_out, bit_extender_1_out[0], bit_extender_2_out[4]);
  Adder #(.width(1)) adder_6 (
    .a(and_14_out), .b(adder_5_cout), .out(adder_6_out), .cin(and_16_out), .cout(adder_6_cout));
  Adder #(.width(1)) adder_7 (
    .a(adder_6_out), .b(adder_6_cout), .out(adder_7_out), .cin(and_18_out), .cout(adder_7_cout));
  Adder #(.width(1)) adder_8 (
    .a(adder_7_out), .b(adder_7_cout), .out(adder_8_out), .cin(and_17_out), .cout(adder_8_cout));
  Adder #(.width(1)) adder_9 (
    .a(adder_8_out), .b(adder_8_cout), .out(adder_9_out), .cin(and_19_out), .cout(adder_9_cout));
  and and_20 (and_20_out, bit_extender_1_out[5], bit_extender_2_out[0]);
  and and_21 (out_4[4], adder_9_out, in_3);
  and and_22 (and_22_out, bit_extender_1_out[4], bit_extender_2_out[1]);
  and and_23 (and_23_out, bit_extender_1_out[3], bit_extender_2_out[2]);
  and and_24 (and_24_out, bit_extender_1_out[2], bit_extender_2_out[3]);
  and and_25 (and_25_out, bit_extender_1_out[1], bit_extender_2_out[4]);
  and and_26 (and_26_out, bit_extender_1_out[0], bit_extender_2_out[5]);
  Adder #(.width(1)) adder_10 (
    .a(and_20_out), .b(adder_9_cout), .out(adder_10_out), .cin(and_22_out), .cout(adder_10_cout));
  Adder #(.width(1)) adder_11 (
    .a(adder_10_out), .b(adder_10_cout), .out(adder_11_out), .cin(and_23_out), .cout(adder_11_cout));
  Adder #(.width(1)) adder_12 (
    .a(adder_11_out), .b(adder_11_cout), .out(adder_12_out), .cin(and_24_out), .cout(adder_12_cout));
  Adder #(.width(1)) adder_13 (
    .a(adder_12_out), .b(adder_12_cout), .out(adder_13_out), .cin(and_25_out), .cout(adder_13_cout));
  Adder #(.width(1)) adder_14 (
    .a(adder_13_out), .b(adder_13_cout), .out(adder_14_out), .cin(and_26_out), .cout(adder_14_cout));
  and and_27 (out_4[5], adder_14_out, in_3);
  and and_28 (and_28_out, bit_extender_1_out[6], bit_extender_2_out[0]);
  and and_29 (and_29_out, bit_extender_1_out[4], bit_extender_2_out[2]);
  and and_30 (and_30_out, bit_extender_1_out[5], bit_extender_2_out[1]);
  and and_31 (and_31_out, bit_extender_1_out[3], bit_extender_2_out[3]);
  and and_32 (and_32_out, bit_extender_1_out[2], bit_extender_2_out[4]);
  and and_33 (and_33_out, bit_extender_1_out[0], bit_extender_2_out[6]);
  and and_34 (and_34_out, bit_extender_1_out[1], bit_extender_2_out[5]);
  Adder #(.width(1)) adder_15 (
    .a(and_28_out), .b(adder_14_cout), .out(adder_15_out), .cin(and_30_out), .cout(adder_15_cout));
  Adder #(.width(1)) adder_16 (
    .a(adder_15_out), .b(adder_15_cout), .out(adder_16_out), .cin(and_29_out), .cout(adder_16_cout));
  Adder #(.width(1)) adder_17 (
    .a(adder_16_out), .b(adder_16_cout), .out(adder_17_out), .cin(and_31_out), .cout(adder_17_cout));
  Adder #(.width(1)) adder_18 (
    .a(adder_17_out), .b(adder_17_cout), .out(adder_18_out), .cin(and_32_out), .cout(adder_18_cout));
  Adder #(.width(1)) adder_19 (
    .a(adder_18_out), .b(adder_18_cout), .out(adder_19_out), .cin(and_34_out), .cout(adder_19_cout));
  Adder #(.width(1)) adder_20 (
    .a(adder_19_out), .b(adder_19_cout), .out(adder_20_out), .cin(and_33_out), .cout(adder_20_cout));
  and and_35 (out_4[6], adder_20_out, in_3);
  and and_36 (and_36_out, bit_extender_1_out[7], bit_extender_2_out[0]);
  and and_37 (and_37_out, bit_extender_1_out[6], bit_extender_2_out[1]);
  and and_38 (and_38_out, bit_extender_1_out[5], bit_extender_2_out[2]);
  and and_39 (and_39_out, bit_extender_1_out[4], bit_extender_2_out[3]);
  and and_40 (and_40_out, bit_extender_1_out[3], bit_extender_2_out[4]);
  and and_41 (and_41_out, bit_extender_1_out[2], bit_extender_2_out[5]);
  and and_42 (and_42_out, bit_extender_1_out[1], bit_extender_2_out[6]);
  and and_43 (and_43_out, bit_extender_1_out[0], bit_extender_2_out[7]);
  Adder #(.width(1)) adder_21 (
    .a(and_36_out), .b(adder_20_cout), .out(adder_21_out), .cin(and_37_out), .cout(adder_21_cout));
  Adder #(.width(1)) adder_22 (
    .a(adder_21_out), .b(adder_21_cout), .out(adder_22_out), .cin(and_38_out), .cout(adder_22_cout));
  Adder #(.width(1)) adder_23 (
    .a(adder_22_out), .b(adder_22_cout), .out(adder_23_out), .cin(and_39_out), .cout(adder_23_cout));
  Adder #(.width(1)) adder_24 (
    .a(adder_23_out), .b(adder_23_cout), .out(adder_24_out), .cin(and_40_out), .cout(adder_24_cout));
  Adder #(.width(1)) adder_25 (
    .a(adder_24_out), .b(adder_24_cout), .out(adder_25_out), .cin(and_41_out), .cout(adder_25_cout));
  Adder #(.width(1)) adder_26 (
    .a(adder_25_out), .b(adder_25_cout), .out(adder_26_out), .cin(and_42_out), .cout(adder_26_cout));
  Adder #(.width(1)) adder_27 (
    .a(adder_26_out), .b(adder_26_cout), .out(adder_27_out), .cin(and_43_out), .cout(adder_27_cout));
  and and_44 (out_4[7], adder_27_out, in_3);
  and and_45 (and_45_out, bit_extender_1_out[8], bit_extender_2_out[0]);
  and and_46 (and_46_out, bit_extender_1_out[7], bit_extender_2_out[1]);
  and and_47 (and_47_out, bit_extender_1_out[6], bit_extender_2_out[2]);
  and and_48 (and_48_out, bit_extender_1_out[5], bit_extender_2_out[3]);
  and and_49 (and_49_out, bit_extender_1_out[4], bit_extender_2_out[4]);
  and and_50 (and_50_out, bit_extender_1_out[3], bit_extender_2_out[5]);
  and and_51 (and_51_out, bit_extender_1_out[2], bit_extender_2_out[6]);
  and and_52 (and_52_out, bit_extender_1_out[1], bit_extender_2_out[7]);
  and and_53 (and_53_out, bit_extender_1_out[0], bit_extender_2_out[8]);
  Adder #(.width(1)) adder_28 (
    .a(and_45_out), .b(adder_27_cout), .out(adder_28_out), .cin(and_46_out), .cout(adder_28_cout));
  Adder #(.width(1)) adder_29 (
    .a(adder_28_out), .b(adder_28_cout), .out(adder_29_out), .cin(and_47_out), .cout(adder_29_cout));
  Adder #(.width(1)) adder_30 (
    .a(adder_29_out), .b(adder_29_cout), .out(adder_30_out), .cin(and_48_out), .cout(adder_30_cout));
  Adder #(.width(1)) adder_31 (
    .a(adder_30_out), .b(adder_30_cout), .out(adder_31_out), .cin(and_49_out), .cout(adder_31_cout));
  Adder #(.width(1)) adder_32 (
    .a(adder_31_out), .b(adder_31_cout), .out(adder_32_out), .cin(and_50_out), .cout(adder_32_cout));
  Adder #(.width(1)) adder_33 (
    .a(adder_32_out), .b(adder_32_cout), .out(adder_33_out), .cin(and_51_out), .cout(adder_33_cout));
  Adder #(.width(1)) adder_34 (
    .a(adder_33_out), .b(adder_33_cout), .out(adder_34_out), .cin(and_52_out), .cout(adder_34_cout));
  Adder #(.width(1)) adder_35 (
    .a(adder_34_out), .b(adder_34_cout), .out(adder_35_out), .cin(and_53_out), .cout(adder_35_cout));
  and and_54 (out_4[8], adder_35_out, in_3);
  and and_55 (and_55_out, bit_extender_1_out[8], bit_extender_2_out[1]);
  and and_56 (and_56_out, bit_extender_1_out[9], bit_extender_2_out[0]);
  and and_57 (and_57_out, bit_extender_1_out[7], bit_extender_2_out[2]);
  and and_58 (and_58_out, bit_extender_1_out[6], bit_extender_2_out[3]);
  and and_59 (and_59_out, bit_extender_1_out[5], bit_extender_2_out[4]);
  and and_60 (and_60_out, bit_extender_1_out[4], bit_extender_2_out[5]);
  and and_61 (and_61_out, bit_extender_1_out[3], bit_extender_2_out[6]);
  and and_62 (and_62_out, bit_extender_1_out[2], bit_extender_2_out[7]);
  and and_63 (and_63_out, bit_extender_1_out[1], bit_extender_2_out[8]);
  and and_64 (and_64_out, bit_extender_1_out[0], bit_extender_2_out[9]);
  Adder #(.width(1)) adder_36 (
    .a(and_56_out), .b(adder_35_cout), .out(adder_36_out), .cin(and_55_out), .cout(adder_36_cout));
  Adder #(.width(1)) adder_37 (
    .a(adder_36_out), .b(adder_36_cout), .out(adder_37_out), .cin(and_57_out), .cout(adder_37_cout));
  Adder #(.width(1)) adder_38 (
    .a(adder_37_out), .b(adder_37_cout), .out(adder_38_out), .cin(and_58_out), .cout(adder_38_cout));
  Adder #(.width(1)) adder_39 (
    .a(adder_38_out), .b(adder_38_cout), .out(adder_39_out), .cin(and_59_out), .cout(adder_39_cout));
  Adder #(.width(1)) adder_40 (
    .a(adder_39_out), .b(adder_39_cout), .out(adder_40_out), .cin(and_60_out), .cout(adder_40_cout));
  Adder #(.width(1)) adder_41 (
    .a(adder_40_out), .b(adder_40_cout), .out(adder_41_out), .cin(and_61_out), .cout(adder_41_cout));
  Adder #(.width(1)) adder_42 (
    .a(adder_41_out), .b(adder_41_cout), .out(adder_42_out), .cin(and_62_out), .cout(adder_42_cout));
  Adder #(.width(1)) adder_43 (
    .a(adder_42_out), .b(adder_42_cout), .out(adder_43_out), .cin(and_63_out), .cout(adder_43_cout));
  and and_65 (and_65_out, bit_extender_1_out[10], bit_extender_2_out[0]);
  Adder #(.width(1)) adder_44 (
    .a(adder_43_out), .b(adder_43_cout), .out(adder_44_out), .cin(and_64_out), .cout(adder_44_cout));
  and and_66 (out_4[9], adder_44_out, in_3);
  and and_67 (and_67_out, bit_extender_1_out[9], bit_extender_2_out[1]);
  and and_68 (and_68_out, bit_extender_1_out[8], bit_extender_2_out[2]);
  and and_69 (and_69_out, bit_extender_1_out[7], bit_extender_2_out[3]);
  and and_70 (and_70_out, bit_extender_1_out[6], bit_extender_2_out[4]);
  and and_71 (and_71_out, bit_extender_1_out[5], bit_extender_2_out[5]);
  and and_72 (and_72_out, bit_extender_1_out[4], bit_extender_2_out[6]);
  and and_73 (and_73_out, bit_extender_1_out[2], bit_extender_2_out[8]);
  and and_74 (and_74_out, bit_extender_1_out[3], bit_extender_2_out[7]);
  and and_75 (and_75_out, bit_extender_1_out[1], bit_extender_2_out[9]);
  and and_76 (and_76_out, bit_extender_1_out[0], bit_extender_2_out[10]);
  Adder #(.width(1)) adder_45 (
    .a(and_65_out), .b(adder_44_cout), .out(adder_45_out), .cin(and_67_out), .cout(adder_45_cout));
  Adder #(.width(1)) adder_46 (
    .a(adder_45_out), .b(adder_45_cout), .out(adder_46_out), .cin(and_68_out), .cout(adder_46_cout));
  Adder #(.width(1)) adder_47 (
    .a(adder_46_out), .b(adder_46_cout), .out(adder_47_out), .cin(and_69_out), .cout(adder_47_cout));
  Adder #(.width(1)) adder_48 (
    .a(adder_47_out), .b(adder_47_cout), .out(adder_48_out), .cin(and_70_out), .cout(adder_48_cout));
  Adder #(.width(1)) adder_49 (
    .a(adder_48_out), .b(adder_48_cout), .out(adder_49_out), .cin(and_71_out), .cout(adder_49_cout));
  Adder #(.width(1)) adder_50 (
    .a(adder_49_out), .b(adder_49_cout), .out(adder_50_out), .cin(and_72_out), .cout(adder_50_cout));
  Adder #(.width(1)) adder_51 (
    .a(adder_50_out), .b(adder_50_cout), .out(adder_51_out), .cin(and_74_out), .cout(adder_51_cout));
  Adder #(.width(1)) adder_52 (
    .a(adder_51_out), .b(adder_51_cout), .out(adder_52_out), .cin(and_73_out), .cout(adder_52_cout));
  Adder #(.width(1)) adder_53 (
    .a(adder_52_out), .b(adder_52_cout), .out(adder_53_out), .cin(and_75_out), .cout(adder_53_cout));
  and and_77 (and_77_out, bit_extender_1_out[11], bit_extender_2_out[0]);
  Adder #(.width(1)) adder_54 (
    .a(adder_53_out), .b(adder_53_cout), .out(adder_54_out), .cin(and_76_out), .cout(adder_54_cout));
  and and_78 (out_4[10], adder_54_out, in_3);
  and and_79 (and_79_out, bit_extender_1_out[10], bit_extender_2_out[1]);
  and and_80 (and_80_out, bit_extender_1_out[9], bit_extender_2_out[2]);
  and and_81 (and_81_out, bit_extender_1_out[8], bit_extender_2_out[3]);
  and and_82 (and_82_out, bit_extender_1_out[7], bit_extender_2_out[4]);
  and and_83 (and_83_out, bit_extender_1_out[6], bit_extender_2_out[5]);
  and and_84 (and_84_out, bit_extender_1_out[5], bit_extender_2_out[6]);
  and and_85 (and_85_out, bit_extender_1_out[3], bit_extender_2_out[8]);
  and and_86 (and_86_out, bit_extender_1_out[4], bit_extender_2_out[7]);
  and and_87 (and_87_out, bit_extender_1_out[2], bit_extender_2_out[9]);
  and and_88 (and_88_out, bit_extender_1_out[1], bit_extender_2_out[10]);
  and and_89 (and_89_out, bit_extender_1_out[0], bit_extender_2_out[11]);
  Adder #(.width(1)) adder_55 (
    .a(and_77_out), .b(adder_54_cout), .out(adder_55_out), .cin(and_79_out), .cout(adder_55_cout));
  Adder #(.width(1)) adder_56 (
    .a(adder_55_out), .b(adder_55_cout), .out(adder_56_out), .cin(and_80_out), .cout(adder_56_cout));
  Adder #(.width(1)) adder_57 (
    .a(adder_56_out), .b(adder_56_cout), .out(adder_57_out), .cin(and_81_out), .cout(adder_57_cout));
  Adder #(.width(1)) adder_58 (
    .a(adder_57_out), .b(adder_57_cout), .out(adder_58_out), .cin(and_82_out), .cout(adder_58_cout));
  Adder #(.width(1)) adder_59 (
    .a(adder_58_out), .b(adder_58_cout), .out(adder_59_out), .cin(and_83_out), .cout(adder_59_cout));
  Adder #(.width(1)) adder_60 (
    .a(adder_59_out), .b(adder_59_cout), .out(adder_60_out), .cin(and_84_out), .cout(adder_60_cout));
  Adder #(.width(1)) adder_61 (
    .a(adder_60_out), .b(adder_60_cout), .out(adder_61_out), .cin(and_86_out), .cout(adder_61_cout));
  Adder #(.width(1)) adder_62 (
    .a(adder_61_out), .b(adder_61_cout), .out(adder_62_out), .cin(and_85_out), .cout(adder_62_cout));
  Adder #(.width(1)) adder_63 (
    .a(adder_62_out), .b(adder_62_cout), .out(adder_63_out), .cin(and_87_out), .cout(adder_63_cout));
  Adder #(.width(1)) adder_64 (
    .a(adder_63_out), .b(adder_63_cout), .out(adder_64_out), .cin(and_88_out), .cout(adder_64_cout));
  Adder #(.width(1)) adder_65 (
    .a(adder_64_out), .b(adder_64_cout), .out(adder_65_out), .cin(and_89_out), .cout(adder_65_cout));
  and and_90 (and_90_out, bit_extender_1_out[12], bit_extender_2_out[0]);
  and and_91 (out_4[11], adder_65_out, in_3);
  and and_92 (and_92_out, bit_extender_1_out[11], bit_extender_2_out[1]);
  and and_93 (and_93_out, bit_extender_1_out[10], bit_extender_2_out[2]);
  and and_94 (and_94_out, bit_extender_1_out[9], bit_extender_2_out[3]);
  and and_95 (and_95_out, bit_extender_1_out[8], bit_extender_2_out[4]);
  and and_96 (and_96_out, bit_extender_1_out[7], bit_extender_2_out[5]);
  and and_97 (and_97_out, bit_extender_1_out[5], bit_extender_2_out[7]);
  and and_98 (and_98_out, bit_extender_1_out[6], bit_extender_2_out[6]);
  and and_99 (and_99_out, bit_extender_1_out[4], bit_extender_2_out[8]);
  and and_100 (and_100_out, bit_extender_1_out[3], bit_extender_2_out[9]);
  and and_101 (and_101_out, bit_extender_1_out[2], bit_extender_2_out[10]);
  and and_102 (and_102_out, bit_extender_1_out[1], bit_extender_2_out[11]);
  and and_103 (and_103_out, bit_extender_1_out[0], bit_extender_2_out[12]);
  Adder #(.width(1)) adder_66 (
    .a(and_90_out), .b(adder_65_cout), .out(adder_66_out), .cin(and_92_out), .cout(adder_66_cout));
  Adder #(.width(1)) adder_67 (
    .a(adder_66_out), .b(adder_66_cout), .out(adder_67_out), .cin(and_93_out), .cout(adder_67_cout));
  Adder #(.width(1)) adder_68 (
    .a(adder_67_out), .b(adder_67_cout), .out(adder_68_out), .cin(and_94_out), .cout(adder_68_cout));
  Adder #(.width(1)) adder_69 (
    .a(adder_68_out), .b(adder_68_cout), .out(adder_69_out), .cin(and_95_out), .cout(adder_69_cout));
  Adder #(.width(1)) adder_70 (
    .a(adder_69_out), .b(adder_69_cout), .out(adder_70_out), .cin(and_96_out), .cout(adder_70_cout));
  Adder #(.width(1)) adder_71 (
    .a(adder_70_out), .b(adder_70_cout), .out(adder_71_out), .cin(and_98_out), .cout(adder_71_cout));
  Adder #(.width(1)) adder_72 (
    .a(adder_71_out), .b(adder_71_cout), .out(adder_72_out), .cin(and_97_out), .cout(adder_72_cout));
  Adder #(.width(1)) adder_73 (
    .a(adder_72_out), .b(adder_72_cout), .out(adder_73_out), .cin(and_99_out), .cout(adder_73_cout));
  Adder #(.width(1)) adder_74 (
    .a(adder_73_out), .b(adder_73_cout), .out(adder_74_out), .cin(and_100_out), .cout(adder_74_cout));
  Adder #(.width(1)) adder_75 (
    .a(adder_74_out), .b(adder_74_cout), .out(adder_75_out), .cin(and_101_out), .cout(adder_75_cout));
  Adder #(.width(1)) adder_76 (
    .a(adder_75_out), .b(adder_75_cout), .out(adder_76_out), .cin(and_102_out), .cout(adder_76_cout));
  Adder #(.width(1)) adder_77 (
    .a(adder_76_out), .b(adder_76_cout), .out(adder_77_out), .cin(and_103_out), .cout(adder_77_cout));
  and and_104 (and_104_out, bit_extender_1_out[13], bit_extender_2_out[0]);
  and and_105 (out_4[12], adder_77_out, in_3);
  and and_106 (and_106_out, bit_extender_1_out[12], bit_extender_2_out[1]);
  and and_107 (and_107_out, bit_extender_1_out[11], bit_extender_2_out[2]);
  and and_108 (and_108_out, bit_extender_1_out[10], bit_extender_2_out[3]);
  and and_109 (and_109_out, bit_extender_1_out[9], bit_extender_2_out[4]);
  and and_110 (and_110_out, bit_extender_1_out[8], bit_extender_2_out[5]);
  and and_111 (and_111_out, bit_extender_1_out[7], bit_extender_2_out[6]);
  and and_112 (and_112_out, bit_extender_1_out[6], bit_extender_2_out[7]);
  and and_113 (and_113_out, bit_extender_1_out[5], bit_extender_2_out[8]);
  and and_114 (and_114_out, bit_extender_1_out[4], bit_extender_2_out[9]);
  and and_115 (and_115_out, bit_extender_1_out[3], bit_extender_2_out[10]);
  and and_116 (and_116_out, bit_extender_1_out[2], bit_extender_2_out[11]);
  and and_117 (and_117_out, bit_extender_1_out[1], bit_extender_2_out[12]);
  and and_118 (and_118_out, bit_extender_1_out[0], bit_extender_2_out[13]);
  Adder #(.width(1)) adder_78 (
    .a(and_104_out), .b(adder_77_cout), .out(adder_78_out), .cin(and_106_out), .cout(adder_78_cout));
  Adder #(.width(1)) adder_79 (
    .a(adder_78_out), .b(adder_78_cout), .out(adder_79_out), .cin(and_107_out), .cout(adder_79_cout));
  Adder #(.width(1)) adder_80 (
    .a(adder_79_out), .b(adder_79_cout), .out(adder_80_out), .cin(and_108_out), .cout(adder_80_cout));
  Adder #(.width(1)) adder_81 (
    .a(adder_80_out), .b(adder_80_cout), .out(adder_81_out), .cin(and_109_out), .cout(adder_81_cout));
  Adder #(.width(1)) adder_82 (
    .a(adder_81_out), .b(adder_81_cout), .out(adder_82_out), .cin(and_110_out), .cout(adder_82_cout));
  Adder #(.width(1)) adder_83 (
    .a(adder_82_out), .b(adder_82_cout), .out(adder_83_out), .cin(and_111_out), .cout(adder_83_cout));
  Adder #(.width(1)) adder_84 (
    .a(adder_83_out), .b(adder_83_cout), .out(adder_84_out), .cin(and_112_out), .cout(adder_84_cout));
  Adder #(.width(1)) adder_85 (
    .a(adder_84_out), .b(adder_84_cout), .out(adder_85_out), .cin(and_113_out), .cout(adder_85_cout));
  Adder #(.width(1)) adder_86 (
    .a(adder_85_out), .b(adder_85_cout), .out(adder_86_out), .cin(and_114_out), .cout(adder_86_cout));
  Adder #(.width(1)) adder_87 (
    .a(adder_86_out), .b(adder_86_cout), .out(adder_87_out), .cin(and_115_out), .cout(adder_87_cout));
  Adder #(.width(1)) adder_88 (
    .a(adder_87_out), .b(adder_87_cout), .out(adder_88_out), .cin(and_116_out), .cout(adder_88_cout));
  Adder #(.width(1)) adder_89 (
    .a(adder_88_out), .b(adder_88_cout), .out(adder_89_out), .cin(and_117_out), .cout(adder_89_cout));
  Adder #(.width(1)) adder_90 (
    .a(adder_89_out), .b(adder_89_cout), .out(adder_90_out), .cin(and_118_out), .cout(adder_90_cout));
  and and_119 (out_4[13], adder_90_out, in_3);
  and and_120 (and_120_out, bit_extender_1_out[13], bit_extender_2_out[1]);
  and and_121 (and_121_out, bit_extender_1_out[14], bit_extender_2_out[0]);
  and and_122 (and_122_out, bit_extender_1_out[12], bit_extender_2_out[2]);
  and and_123 (and_123_out, bit_extender_1_out[11], bit_extender_2_out[3]);
  and and_124 (and_124_out, bit_extender_1_out[9], bit_extender_2_out[5]);
  and and_125 (and_125_out, bit_extender_1_out[10], bit_extender_2_out[4]);
  and and_126 (and_126_out, bit_extender_1_out[8], bit_extender_2_out[6]);
  and and_127 (and_127_out, bit_extender_1_out[7], bit_extender_2_out[7]);
  and and_128 (and_128_out, bit_extender_1_out[6], bit_extender_2_out[8]);
  and and_129 (and_129_out, bit_extender_1_out[5], bit_extender_2_out[9]);
  and and_130 (and_130_out, bit_extender_1_out[4], bit_extender_2_out[10]);
  and and_131 (and_131_out, bit_extender_1_out[3], bit_extender_2_out[11]);
  and and_132 (and_132_out, bit_extender_1_out[1], bit_extender_2_out[13]);
  and and_133 (and_133_out, bit_extender_1_out[2], bit_extender_2_out[12]);
  and and_134 (and_134_out, bit_extender_1_out[0], bit_extender_2_out[14]);
  Adder #(.width(1)) adder_91 (
    .a(and_121_out), .b(adder_90_cout), .out(adder_91_out), .cin(and_120_out), .cout(adder_91_cout));
  Adder #(.width(1)) adder_92 (
    .a(adder_91_out), .b(adder_91_cout), .out(adder_92_out), .cin(and_122_out), .cout(adder_92_cout));
  Adder #(.width(1)) adder_93 (
    .a(adder_92_out), .b(adder_92_cout), .out(adder_93_out), .cin(and_123_out), .cout(adder_93_cout));
  Adder #(.width(1)) adder_94 (
    .a(adder_93_out), .b(adder_93_cout), .out(adder_94_out), .cin(and_125_out), .cout(adder_94_cout));
  Adder #(.width(1)) adder_95 (
    .a(adder_94_out), .b(adder_94_cout), .out(adder_95_out), .cin(and_124_out), .cout(adder_95_cout));
  Adder #(.width(1)) adder_96 (
    .a(adder_95_out), .b(adder_95_cout), .out(adder_96_out), .cin(and_126_out), .cout(adder_96_cout));
  Adder #(.width(1)) adder_97 (
    .a(adder_96_out), .b(adder_96_cout), .out(adder_97_out), .cin(and_127_out), .cout(adder_97_cout));
  Adder #(.width(1)) adder_98 (
    .a(adder_97_out), .b(adder_97_cout), .out(adder_98_out), .cin(and_128_out), .cout(adder_98_cout));
  Adder #(.width(1)) adder_99 (
    .a(adder_98_out), .b(adder_98_cout), .out(adder_99_out), .cin(and_129_out), .cout(adder_99_cout));
  Adder #(.width(1)) adder_100 (
    .a(adder_99_out), .b(adder_99_cout), .out(adder_100_out), .cin(and_130_out), .cout(adder_100_cout));
  Adder #(.width(1)) adder_101 (
    .a(adder_100_out), .b(adder_100_cout), .out(adder_101_out), .cin(and_131_out), .cout(adder_101_cout));
  Adder #(.width(1)) adder_102 (
    .a(adder_101_out), .b(adder_101_cout), .out(adder_102_out), .cin(and_133_out), .cout(adder_102_cout));
  Adder #(.width(1)) adder_103 (
    .a(adder_102_out), .b(adder_102_cout), .out(adder_103_out), .cin(and_132_out), .cout(adder_103_cout));
  Adder #(.width(1)) adder_104 (
    .a(adder_103_out), .b(adder_103_cout), .out(adder_104_out), .cin(and_134_out), .cout(adder_104_cout));
  and and_135 (out_4[14], adder_104_out, in_3);
  and and_136 (and_136_out, bit_extender_1_out[15], bit_extender_2_out[0]);
  and and_137 (and_137_out, bit_extender_1_out[14], bit_extender_2_out[1]);
  and and_138 (and_138_out, bit_extender_1_out[13], bit_extender_2_out[2]);
  and and_139 (and_139_out, bit_extender_1_out[12], bit_extender_2_out[3]);
  and and_140 (and_140_out, bit_extender_1_out[11], bit_extender_2_out[4]);
  and and_141 (and_141_out, bit_extender_1_out[9], bit_extender_2_out[6]);
  and and_142 (and_142_out, bit_extender_1_out[10], bit_extender_2_out[5]);
  and and_143 (and_143_out, bit_extender_1_out[8], bit_extender_2_out[7]);
  and and_144 (and_144_out, bit_extender_1_out[7], bit_extender_2_out[8]);
  and and_145 (and_145_out, bit_extender_1_out[5], bit_extender_2_out[10]);
  and and_146 (and_146_out, bit_extender_1_out[6], bit_extender_2_out[9]);
  and and_147 (and_147_out, bit_extender_1_out[4], bit_extender_2_out[11]);
  and and_148 (and_148_out, bit_extender_1_out[3], bit_extender_2_out[12]);
  and and_149 (and_149_out, bit_extender_1_out[2], bit_extender_2_out[13]);
  and and_150 (and_150_out, bit_extender_1_out[1], bit_extender_2_out[14]);
  and and_151 (and_151_out, bit_extender_1_out[0], bit_extender_2_out[15]);
  Adder #(.width(1)) adder_105 (
    .a(and_136_out), .b(adder_104_cout), .out(adder_105_out), .cin(and_137_out), .cout(adder_105_cout));
  Adder #(.width(1)) adder_106 (
    .a(adder_105_out), .b(adder_105_cout), .out(adder_106_out), .cin(and_138_out), .cout(adder_106_cout));
  Adder #(.width(1)) adder_107 (
    .a(adder_106_out), .b(adder_106_cout), .out(adder_107_out), .cin(and_139_out), .cout(adder_107_cout));
  Adder #(.width(1)) adder_108 (
    .a(adder_107_out), .b(adder_107_cout), .out(adder_108_out), .cin(and_140_out), .cout(adder_108_cout));
  Adder #(.width(1)) adder_109 (
    .a(adder_108_out), .b(adder_108_cout), .out(adder_109_out), .cin(and_142_out), .cout(adder_109_cout));
  Adder #(.width(1)) adder_110 (
    .a(adder_109_out), .b(adder_109_cout), .out(adder_110_out), .cin(and_141_out), .cout(adder_110_cout));
  Adder #(.width(1)) adder_111 (
    .a(adder_110_out), .b(adder_110_cout), .out(adder_111_out), .cin(and_143_out), .cout(adder_111_cout));
  Adder #(.width(1)) adder_112 (
    .a(adder_111_out), .b(adder_111_cout), .out(adder_112_out), .cin(and_144_out), .cout(adder_112_cout));
  Adder #(.width(1)) adder_113 (
    .a(adder_112_out), .b(adder_112_cout), .out(adder_113_out), .cin(and_146_out), .cout(adder_113_cout));
  Adder #(.width(1)) adder_114 (
    .a(adder_113_out), .b(adder_113_cout), .out(adder_114_out), .cin(and_145_out), .cout(adder_114_cout));
  Adder #(.width(1)) adder_115 (
    .a(adder_114_out), .b(adder_114_cout), .out(adder_115_out), .cin(and_147_out), .cout(adder_115_cout));
  Adder #(.width(1)) adder_116 (
    .a(adder_115_out), .b(adder_115_cout), .out(adder_116_out), .cin(and_148_out), .cout(adder_116_cout));
  Adder #(.width(1)) adder_117 (
    .a(adder_116_out), .b(adder_116_cout), .out(adder_117_out), .cin(and_149_out), .cout(adder_117_cout));
  Adder #(.width(1)) adder_118 (
    .a(adder_117_out), .b(adder_117_cout), .out(adder_118_out), .cin(and_150_out), .cout(adder_118_cout));
  Adder #(.width(1)) adder_119 (
    .a(adder_118_out), .b(adder_118_cout), .out(adder_119_out), .cin(and_151_out), .cout(adder_119_cout));
  and and_152 (out_4[15], adder_119_out, in_3);
  and and_153 (and_153_out, bit_extender_1_out[15], bit_extender_2_out[1]);
  and and_154 (and_154_out, bit_extender_1_out[14], bit_extender_2_out[2]);
  and and_155 (and_155_out, bit_extender_1_out[13], bit_extender_2_out[3]);
  and and_156 (and_156_out, bit_extender_1_out[12], bit_extender_2_out[4]);
  and and_157 (and_157_out, bit_extender_1_out[11], bit_extender_2_out[5]);
  and and_158 (and_158_out, bit_extender_1_out[10], bit_extender_2_out[6]);
  and and_159 (and_159_out, bit_extender_1_out[9], bit_extender_2_out[7]);
  and and_160 (and_160_out, bit_extender_1_out[8], bit_extender_2_out[8]);
  and and_161 (and_161_out, bit_extender_1_out[7], bit_extender_2_out[9]);
  and and_162 (and_162_out, bit_extender_1_out[6], bit_extender_2_out[10]);
  and and_163 (and_163_out, bit_extender_1_out[5], bit_extender_2_out[11]);
  and and_164 (and_164_out, bit_extender_1_out[4], bit_extender_2_out[12]);
  and and_165 (and_165_out, bit_extender_1_out[2], bit_extender_2_out[14]);
  and and_166 (and_166_out, bit_extender_1_out[3], bit_extender_2_out[13]);
  and and_167 (and_167_out, bit_extender_1_out[1], bit_extender_2_out[15]);
  Adder #(.width(1)) adder_120 (
    .a(and_153_out), .b(adder_119_cout), .out(adder_120_out), .cin(and_154_out), .cout(adder_120_cout));
  Adder #(.width(1)) adder_121 (
    .a(adder_120_out), .b(adder_120_cout), .out(adder_121_out), .cin(and_155_out), .cout(adder_121_cout));
  Adder #(.width(1)) adder_122 (
    .a(adder_121_out), .b(adder_121_cout), .out(adder_122_out), .cin(and_156_out), .cout(adder_122_cout));
  Adder #(.width(1)) adder_123 (
    .a(adder_122_out), .b(adder_122_cout), .out(adder_123_out), .cin(and_157_out), .cout(adder_123_cout));
  Adder #(.width(1)) adder_124 (
    .a(adder_123_out), .b(adder_123_cout), .out(adder_124_out), .cin(and_158_out), .cout(adder_124_cout));
  Adder #(.width(1)) adder_125 (
    .a(adder_124_out), .b(adder_124_cout), .out(adder_125_out), .cin(and_159_out), .cout(adder_125_cout));
  Adder #(.width(1)) adder_126 (
    .a(adder_125_out), .b(adder_125_cout), .out(adder_126_out), .cin(and_160_out), .cout(adder_126_cout));
  Adder #(.width(1)) adder_127 (
    .a(adder_126_out), .b(adder_126_cout), .out(adder_127_out), .cin(and_161_out), .cout(adder_127_cout));
  Adder #(.width(1)) adder_128 (
    .a(adder_127_out), .b(adder_127_cout), .out(adder_128_out), .cin(and_162_out), .cout(adder_128_cout));
  Adder #(.width(1)) adder_129 (
    .a(adder_128_out), .b(adder_128_cout), .out(adder_129_out), .cin(and_163_out), .cout(adder_129_cout));
  Adder #(.width(1)) adder_130 (
    .a(adder_129_out), .b(adder_129_cout), .out(adder_130_out), .cin(and_164_out), .cout(adder_130_cout));
  Adder #(.width(1)) adder_131 (
    .a(adder_130_out), .b(adder_130_cout), .out(adder_131_out), .cin(and_166_out), .cout(adder_131_cout));
  Adder #(.width(1)) adder_132 (
    .a(adder_131_out), .b(adder_131_cout), .out(adder_132_out), .cin(and_165_out), .cout(adder_132_cout));
  Adder #(.width(1)) adder_133 (
    .a(adder_132_out), .b(adder_132_cout), .out(adder_133_out), .cin(and_167_out), .cout(adder_133_cout));
  and and_168 (out_4[16], adder_133_out, in_3);
  and and_169 (and_169_out, bit_extender_1_out[15], bit_extender_2_out[2]);
  and and_170 (and_170_out, bit_extender_1_out[14], bit_extender_2_out[3]);
  and and_171 (and_171_out, bit_extender_1_out[13], bit_extender_2_out[4]);
  and and_172 (and_172_out, bit_extender_1_out[12], bit_extender_2_out[5]);
  and and_173 (and_173_out, bit_extender_1_out[11], bit_extender_2_out[6]);
  and and_174 (and_174_out, bit_extender_1_out[10], bit_extender_2_out[7]);
  and and_175 (and_175_out, bit_extender_1_out[9], bit_extender_2_out[8]);
  and and_176 (and_176_out, bit_extender_1_out[8], bit_extender_2_out[9]);
  and and_177 (and_177_out, bit_extender_1_out[7], bit_extender_2_out[10]);
  and and_178 (and_178_out, bit_extender_1_out[6], bit_extender_2_out[11]);
  and and_179 (and_179_out, bit_extender_1_out[5], bit_extender_2_out[12]);
  and and_180 (and_180_out, bit_extender_1_out[4], bit_extender_2_out[13]);
  and and_181 (and_181_out, bit_extender_1_out[3], bit_extender_2_out[14]);
  and and_182 (and_182_out, bit_extender_1_out[2], bit_extender_2_out[15]);
  Adder #(.width(1)) adder_134 (
    .a(and_169_out), .b(adder_133_cout), .out(adder_134_out), .cin(and_170_out), .cout(adder_134_cout));
  Adder #(.width(1)) adder_135 (
    .a(adder_134_out), .b(adder_134_cout), .out(adder_135_out), .cin(and_171_out), .cout(adder_135_cout));
  Adder #(.width(1)) adder_136 (
    .a(adder_135_out), .b(adder_135_cout), .out(adder_136_out), .cin(and_172_out), .cout(adder_136_cout));
  Adder #(.width(1)) adder_137 (
    .a(adder_136_out), .b(adder_136_cout), .out(adder_137_out), .cin(and_173_out), .cout(adder_137_cout));
  Adder #(.width(1)) adder_138 (
    .a(adder_137_out), .b(adder_137_cout), .out(adder_138_out), .cin(and_174_out), .cout(adder_138_cout));
  Adder #(.width(1)) adder_139 (
    .a(adder_138_out), .b(adder_138_cout), .out(adder_139_out), .cin(and_175_out), .cout(adder_139_cout));
  Adder #(.width(1)) adder_140 (
    .a(adder_139_out), .b(adder_139_cout), .out(adder_140_out), .cin(and_176_out), .cout(adder_140_cout));
  Adder #(.width(1)) adder_141 (
    .a(adder_140_out), .b(adder_140_cout), .out(adder_141_out), .cin(and_177_out), .cout(adder_141_cout));
  Adder #(.width(1)) adder_142 (
    .a(adder_141_out), .b(adder_141_cout), .out(adder_142_out), .cin(and_178_out), .cout(adder_142_cout));
  Adder #(.width(1)) adder_143 (
    .a(adder_142_out), .b(adder_142_cout), .out(adder_143_out), .cin(and_179_out), .cout(adder_143_cout));
  Adder #(.width(1)) adder_144 (
    .a(adder_143_out), .b(adder_143_cout), .out(adder_144_out), .cin(and_180_out), .cout(adder_144_cout));
  Adder #(.width(1)) adder_145 (
    .a(adder_144_out), .b(adder_144_cout), .out(adder_145_out), .cin(and_181_out), .cout(adder_145_cout));
  Adder #(.width(1)) adder_146 (
    .a(adder_145_out), .b(adder_145_cout), .out(adder_146_out), .cin(and_182_out), .cout(adder_146_cout));
  and and_183 (out_4[17], adder_146_out, in_3);
  and and_184 (and_184_out, bit_extender_1_out[14], bit_extender_2_out[4]);
  and and_185 (and_185_out, bit_extender_1_out[15], bit_extender_2_out[3]);
  and and_186 (and_186_out, bit_extender_1_out[13], bit_extender_2_out[5]);
  and and_187 (and_187_out, bit_extender_1_out[12], bit_extender_2_out[6]);
  and and_188 (and_188_out, bit_extender_1_out[11], bit_extender_2_out[7]);
  and and_189 (and_189_out, bit_extender_1_out[10], bit_extender_2_out[8]);
  and and_190 (and_190_out, bit_extender_1_out[9], bit_extender_2_out[9]);
  and and_191 (and_191_out, bit_extender_1_out[8], bit_extender_2_out[10]);
  and and_192 (and_192_out, bit_extender_1_out[7], bit_extender_2_out[11]);
  and and_193 (and_193_out, bit_extender_1_out[6], bit_extender_2_out[12]);
  and and_194 (and_194_out, bit_extender_1_out[5], bit_extender_2_out[13]);
  and and_195 (and_195_out, bit_extender_1_out[4], bit_extender_2_out[14]);
  and and_196 (and_196_out, bit_extender_1_out[3], bit_extender_2_out[15]);
  Adder #(.width(1)) adder_147 (
    .a(and_185_out), .b(adder_146_cout), .out(adder_147_out), .cin(and_184_out), .cout(adder_147_cout));
  Adder #(.width(1)) adder_148 (
    .a(adder_147_out), .b(adder_147_cout), .out(adder_148_out), .cin(and_186_out), .cout(adder_148_cout));
  Adder #(.width(1)) adder_149 (
    .a(adder_148_out), .b(adder_148_cout), .out(adder_149_out), .cin(and_187_out), .cout(adder_149_cout));
  Adder #(.width(1)) adder_150 (
    .a(adder_149_out), .b(adder_149_cout), .out(adder_150_out), .cin(and_188_out), .cout(adder_150_cout));
  Adder #(.width(1)) adder_151 (
    .a(adder_150_out), .b(adder_150_cout), .out(adder_151_out), .cin(and_189_out), .cout(adder_151_cout));
  Adder #(.width(1)) adder_152 (
    .a(adder_151_out), .b(adder_151_cout), .out(adder_152_out), .cin(and_190_out), .cout(adder_152_cout));
  Adder #(.width(1)) adder_153 (
    .a(adder_152_out), .b(adder_152_cout), .out(adder_153_out), .cin(and_191_out), .cout(adder_153_cout));
  Adder #(.width(1)) adder_154 (
    .a(adder_153_out), .b(adder_153_cout), .out(adder_154_out), .cin(and_192_out), .cout(adder_154_cout));
  Adder #(.width(1)) adder_155 (
    .a(adder_154_out), .b(adder_154_cout), .out(adder_155_out), .cin(and_193_out), .cout(adder_155_cout));
  Adder #(.width(1)) adder_156 (
    .a(adder_155_out), .b(adder_155_cout), .out(adder_156_out), .cin(and_194_out), .cout(adder_156_cout));
  Adder #(.width(1)) adder_157 (
    .a(adder_156_out), .b(adder_156_cout), .out(adder_157_out), .cin(and_195_out), .cout(adder_157_cout));
  Adder #(.width(1)) adder_158 (
    .a(adder_157_out), .b(adder_157_cout), .out(adder_158_out), .cin(and_196_out), .cout(adder_158_cout));
  and and_197 (out_4[18], adder_158_out, in_3);
  and and_198 (and_198_out, bit_extender_1_out[15], bit_extender_2_out[4]);
  and and_199 (and_199_out, bit_extender_1_out[14], bit_extender_2_out[5]);
  and and_200 (and_200_out, bit_extender_1_out[13], bit_extender_2_out[6]);
  and and_201 (and_201_out, bit_extender_1_out[12], bit_extender_2_out[7]);
  and and_202 (and_202_out, bit_extender_1_out[11], bit_extender_2_out[8]);
  and and_203 (and_203_out, bit_extender_1_out[10], bit_extender_2_out[9]);
  and and_204 (and_204_out, bit_extender_1_out[9], bit_extender_2_out[10]);
  and and_205 (and_205_out, bit_extender_1_out[8], bit_extender_2_out[11]);
  and and_206 (and_206_out, bit_extender_1_out[6], bit_extender_2_out[13]);
  and and_207 (and_207_out, bit_extender_1_out[7], bit_extender_2_out[12]);
  and and_208 (and_208_out, bit_extender_1_out[5], bit_extender_2_out[14]);
  and and_209 (and_209_out, bit_extender_1_out[4], bit_extender_2_out[15]);
  Adder #(.width(1)) adder_159 (
    .a(and_198_out), .b(adder_158_cout), .out(adder_159_out), .cin(and_199_out), .cout(adder_159_cout));
  Adder #(.width(1)) adder_160 (
    .a(adder_159_out), .b(adder_159_cout), .out(adder_160_out), .cin(and_200_out), .cout(adder_160_cout));
  Adder #(.width(1)) adder_161 (
    .a(adder_160_out), .b(adder_160_cout), .out(adder_161_out), .cin(and_201_out), .cout(adder_161_cout));
  Adder #(.width(1)) adder_162 (
    .a(adder_161_out), .b(adder_161_cout), .out(adder_162_out), .cin(and_202_out), .cout(adder_162_cout));
  Adder #(.width(1)) adder_163 (
    .a(adder_162_out), .b(adder_162_cout), .out(adder_163_out), .cin(and_203_out), .cout(adder_163_cout));
  Adder #(.width(1)) adder_164 (
    .a(adder_163_out), .b(adder_163_cout), .out(adder_164_out), .cin(and_204_out), .cout(adder_164_cout));
  Adder #(.width(1)) adder_165 (
    .a(adder_164_out), .b(adder_164_cout), .out(adder_165_out), .cin(and_205_out), .cout(adder_165_cout));
  Adder #(.width(1)) adder_166 (
    .a(adder_165_out), .b(adder_165_cout), .out(adder_166_out), .cin(and_207_out), .cout(adder_166_cout));
  Adder #(.width(1)) adder_167 (
    .a(adder_166_out), .b(adder_166_cout), .out(adder_167_out), .cin(and_206_out), .cout(adder_167_cout));
  Adder #(.width(1)) adder_168 (
    .a(adder_167_out), .b(adder_167_cout), .out(adder_168_out), .cin(and_208_out), .cout(adder_168_cout));
  and and_210 (and_210_out, bit_extender_1_out[15], bit_extender_2_out[5]);
  Adder #(.width(1)) adder_169 (
    .a(adder_168_out), .b(adder_168_cout), .out(adder_169_out), .cin(and_209_out), .cout(adder_169_cout));
  and and_211 (out_4[19], adder_169_out, in_3);
  and and_212 (and_212_out, bit_extender_1_out[14], bit_extender_2_out[6]);
  and and_213 (and_213_out, bit_extender_1_out[13], bit_extender_2_out[7]);
  and and_214 (and_214_out, bit_extender_1_out[12], bit_extender_2_out[8]);
  and and_215 (and_215_out, bit_extender_1_out[11], bit_extender_2_out[9]);
  and and_216 (and_216_out, bit_extender_1_out[10], bit_extender_2_out[10]);
  and and_217 (and_217_out, bit_extender_1_out[9], bit_extender_2_out[11]);
  and and_218 (and_218_out, bit_extender_1_out[7], bit_extender_2_out[13]);
  and and_219 (and_219_out, bit_extender_1_out[8], bit_extender_2_out[12]);
  and and_220 (and_220_out, bit_extender_1_out[6], bit_extender_2_out[14]);
  and and_221 (and_221_out, bit_extender_1_out[5], bit_extender_2_out[15]);
  Adder #(.width(1)) adder_170 (
    .a(and_210_out), .b(adder_169_cout), .out(adder_170_out), .cin(and_212_out), .cout(adder_170_cout));
  Adder #(.width(1)) adder_171 (
    .a(adder_170_out), .b(adder_170_cout), .out(adder_171_out), .cin(and_213_out), .cout(adder_171_cout));
  Adder #(.width(1)) adder_172 (
    .a(adder_171_out), .b(adder_171_cout), .out(adder_172_out), .cin(and_214_out), .cout(adder_172_cout));
  Adder #(.width(1)) adder_173 (
    .a(adder_172_out), .b(adder_172_cout), .out(adder_173_out), .cin(and_215_out), .cout(adder_173_cout));
  Adder #(.width(1)) adder_174 (
    .a(adder_173_out), .b(adder_173_cout), .out(adder_174_out), .cin(and_216_out), .cout(adder_174_cout));
  Adder #(.width(1)) adder_175 (
    .a(adder_174_out), .b(adder_174_cout), .out(adder_175_out), .cin(and_217_out), .cout(adder_175_cout));
  Adder #(.width(1)) adder_176 (
    .a(adder_175_out), .b(adder_175_cout), .out(adder_176_out), .cin(and_219_out), .cout(adder_176_cout));
  Adder #(.width(1)) adder_177 (
    .a(adder_176_out), .b(adder_176_cout), .out(adder_177_out), .cin(and_218_out), .cout(adder_177_cout));
  Adder #(.width(1)) adder_178 (
    .a(adder_177_out), .b(adder_177_cout), .out(adder_178_out), .cin(and_220_out), .cout(adder_178_cout));
  Adder #(.width(1)) adder_179 (
    .a(adder_178_out), .b(adder_178_cout), .out(adder_179_out), .cin(and_221_out), .cout(adder_179_cout));
  and and_222 (out_4[20], adder_179_out, in_3);
  and and_223 (and_223_out, bit_extender_1_out[15], bit_extender_2_out[6]);
  and and_224 (and_224_out, bit_extender_1_out[14], bit_extender_2_out[7]);
  and and_225 (and_225_out, bit_extender_1_out[13], bit_extender_2_out[8]);
  and and_226 (and_226_out, bit_extender_1_out[12], bit_extender_2_out[9]);
  and and_227 (and_227_out, bit_extender_1_out[10], bit_extender_2_out[11]);
  and and_228 (and_228_out, bit_extender_1_out[11], bit_extender_2_out[10]);
  and and_229 (and_229_out, bit_extender_1_out[9], bit_extender_2_out[12]);
  and and_230 (and_230_out, bit_extender_1_out[8], bit_extender_2_out[13]);
  and and_231 (and_231_out, bit_extender_1_out[7], bit_extender_2_out[14]);
  and and_232 (and_232_out, bit_extender_1_out[6], bit_extender_2_out[15]);
  Adder #(.width(1)) adder_180 (
    .a(and_223_out), .b(adder_179_cout), .out(adder_180_out), .cin(and_224_out), .cout(adder_180_cout));
  Adder #(.width(1)) adder_181 (
    .a(adder_180_out), .b(adder_180_cout), .out(adder_181_out), .cin(and_225_out), .cout(adder_181_cout));
  Adder #(.width(1)) adder_182 (
    .a(adder_181_out), .b(adder_181_cout), .out(adder_182_out), .cin(and_226_out), .cout(adder_182_cout));
  Adder #(.width(1)) adder_183 (
    .a(adder_182_out), .b(adder_182_cout), .out(adder_183_out), .cin(and_228_out), .cout(adder_183_cout));
  Adder #(.width(1)) adder_184 (
    .a(adder_183_out), .b(adder_183_cout), .out(adder_184_out), .cin(and_227_out), .cout(adder_184_cout));
  Adder #(.width(1)) adder_185 (
    .a(adder_184_out), .b(adder_184_cout), .out(adder_185_out), .cin(and_229_out), .cout(adder_185_cout));
  Adder #(.width(1)) adder_186 (
    .a(adder_185_out), .b(adder_185_cout), .out(adder_186_out), .cin(and_230_out), .cout(adder_186_cout));
  Adder #(.width(1)) adder_187 (
    .a(adder_186_out), .b(adder_186_cout), .out(adder_187_out), .cin(and_231_out), .cout(adder_187_cout));
  Adder #(.width(1)) adder_188 (
    .a(adder_187_out), .b(adder_187_cout), .out(adder_188_out), .cin(and_232_out), .cout(adder_188_cout));
  and and_233 (and_233_out, bit_extender_1_out[15], bit_extender_2_out[7]);
  and and_234 (out_4[21], adder_188_out, in_3);
  and and_235 (and_235_out, bit_extender_1_out[14], bit_extender_2_out[8]);
  and and_236 (and_236_out, bit_extender_1_out[13], bit_extender_2_out[9]);
  and and_237 (and_237_out, bit_extender_1_out[12], bit_extender_2_out[10]);
  and and_238 (and_238_out, bit_extender_1_out[11], bit_extender_2_out[11]);
  and and_239 (and_239_out, bit_extender_1_out[10], bit_extender_2_out[12]);
  and and_240 (and_240_out, bit_extender_1_out[8], bit_extender_2_out[14]);
  and and_241 (and_241_out, bit_extender_1_out[9], bit_extender_2_out[13]);
  and and_242 (and_242_out, bit_extender_1_out[7], bit_extender_2_out[15]);
  Adder #(.width(1)) adder_189 (
    .a(and_233_out), .b(adder_188_cout), .out(adder_189_out), .cin(and_235_out), .cout(adder_189_cout));
  Adder #(.width(1)) adder_190 (
    .a(adder_189_out), .b(adder_189_cout), .out(adder_190_out), .cin(and_236_out), .cout(adder_190_cout));
  Adder #(.width(1)) adder_191 (
    .a(adder_190_out), .b(adder_190_cout), .out(adder_191_out), .cin(and_237_out), .cout(adder_191_cout));
  Adder #(.width(1)) adder_192 (
    .a(adder_191_out), .b(adder_191_cout), .out(adder_192_out), .cin(and_238_out), .cout(adder_192_cout));
  Adder #(.width(1)) adder_193 (
    .a(adder_192_out), .b(adder_192_cout), .out(adder_193_out), .cin(and_239_out), .cout(adder_193_cout));
  Adder #(.width(1)) adder_194 (
    .a(adder_193_out), .b(adder_193_cout), .out(adder_194_out), .cin(and_241_out), .cout(adder_194_cout));
  Adder #(.width(1)) adder_195 (
    .a(adder_194_out), .b(adder_194_cout), .out(adder_195_out), .cin(and_240_out), .cout(adder_195_cout));
  and and_243 (and_243_out, bit_extender_1_out[15], bit_extender_2_out[8]);
  Adder #(.width(1)) adder_196 (
    .a(adder_195_out), .b(adder_195_cout), .out(adder_196_out), .cin(and_242_out), .cout(adder_196_cout));
  and and_244 (out_4[22], adder_196_out, in_3);
  and and_245 (and_245_out, bit_extender_1_out[14], bit_extender_2_out[9]);
  and and_246 (and_246_out, bit_extender_1_out[13], bit_extender_2_out[10]);
  and and_247 (and_247_out, bit_extender_1_out[12], bit_extender_2_out[11]);
  and and_248 (and_248_out, bit_extender_1_out[11], bit_extender_2_out[12]);
  and and_249 (and_249_out, bit_extender_1_out[10], bit_extender_2_out[13]);
  and and_250 (and_250_out, bit_extender_1_out[9], bit_extender_2_out[14]);
  and and_251 (and_251_out, bit_extender_1_out[8], bit_extender_2_out[15]);
  Adder #(.width(1)) adder_197 (
    .a(and_243_out), .b(adder_196_cout), .out(adder_197_out), .cin(and_245_out), .cout(adder_197_cout));
  Adder #(.width(1)) adder_198 (
    .a(adder_197_out), .b(adder_197_cout), .out(adder_198_out), .cin(and_246_out), .cout(adder_198_cout));
  Adder #(.width(1)) adder_199 (
    .a(adder_198_out), .b(adder_198_cout), .out(adder_199_out), .cin(and_247_out), .cout(adder_199_cout));
  Adder #(.width(1)) adder_200 (
    .a(adder_199_out), .b(adder_199_cout), .out(adder_200_out), .cin(and_248_out), .cout(adder_200_cout));
  Adder #(.width(1)) adder_201 (
    .a(adder_200_out), .b(adder_200_cout), .out(adder_201_out), .cin(and_249_out), .cout(adder_201_cout));
  Adder #(.width(1)) adder_202 (
    .a(adder_201_out), .b(adder_201_cout), .out(adder_202_out), .cin(and_250_out), .cout(adder_202_cout));
  Adder #(.width(1)) adder_203 (
    .a(adder_202_out), .b(adder_202_cout), .out(adder_203_out), .cin(and_251_out), .cout(adder_203_cout));
  and and_252 (out_4[23], adder_203_out, in_3);
  and and_253 (and_253_out, bit_extender_1_out[15], bit_extender_2_out[9]);
  and and_254 (and_254_out, bit_extender_1_out[13], bit_extender_2_out[11]);
  and and_255 (and_255_out, bit_extender_1_out[14], bit_extender_2_out[10]);
  and and_256 (and_256_out, bit_extender_1_out[12], bit_extender_2_out[12]);
  and and_257 (and_257_out, bit_extender_1_out[11], bit_extender_2_out[13]);
  and and_258 (and_258_out, bit_extender_1_out[10], bit_extender_2_out[14]);
  and and_259 (and_259_out, bit_extender_1_out[9], bit_extender_2_out[15]);
  Adder #(.width(1)) adder_204 (
    .a(and_253_out), .b(adder_203_cout), .out(adder_204_out), .cin(and_255_out), .cout(adder_204_cout));
  Adder #(.width(1)) adder_205 (
    .a(adder_204_out), .b(adder_204_cout), .out(adder_205_out), .cin(and_254_out), .cout(adder_205_cout));
  Adder #(.width(1)) adder_206 (
    .a(adder_205_out), .b(adder_205_cout), .out(adder_206_out), .cin(and_256_out), .cout(adder_206_cout));
  Adder #(.width(1)) adder_207 (
    .a(adder_206_out), .b(adder_206_cout), .out(adder_207_out), .cin(and_257_out), .cout(adder_207_cout));
  Adder #(.width(1)) adder_208 (
    .a(adder_207_out), .b(adder_207_cout), .out(adder_208_out), .cin(and_258_out), .cout(adder_208_cout));
  Adder #(.width(1)) adder_209 (
    .a(adder_208_out), .b(adder_208_cout), .out(adder_209_out), .cin(and_259_out), .cout(adder_209_cout));
  and and_260 (and_260_out, bit_extender_1_out[15], bit_extender_2_out[10]);
  and and_261 (out_4[24], adder_209_out, in_3);
  and and_262 (and_262_out, bit_extender_1_out[14], bit_extender_2_out[11]);
  and and_263 (and_263_out, bit_extender_1_out[12], bit_extender_2_out[13]);
  and and_264 (and_264_out, bit_extender_1_out[13], bit_extender_2_out[12]);
  and and_265 (and_265_out, bit_extender_1_out[11], bit_extender_2_out[14]);
  and and_266 (and_266_out, bit_extender_1_out[10], bit_extender_2_out[15]);
  Adder #(.width(1)) adder_210 (
    .a(and_260_out), .b(adder_209_cout), .out(adder_210_out), .cin(and_262_out), .cout(adder_210_cout));
  Adder #(.width(1)) adder_211 (
    .a(adder_210_out), .b(adder_210_cout), .out(adder_211_out), .cin(and_264_out), .cout(adder_211_cout));
  Adder #(.width(1)) adder_212 (
    .a(adder_211_out), .b(adder_211_cout), .out(adder_212_out), .cin(and_263_out), .cout(adder_212_cout));
  Adder #(.width(1)) adder_213 (
    .a(adder_212_out), .b(adder_212_cout), .out(adder_213_out), .cin(and_265_out), .cout(adder_213_cout));
  Adder #(.width(1)) adder_214 (
    .a(adder_213_out), .b(adder_213_cout), .out(adder_214_out), .cin(and_266_out), .cout(adder_214_cout));
  and and_267 (out_4[25], adder_214_out, in_3);
  and and_268 (and_268_out, bit_extender_1_out[14], bit_extender_2_out[12]);
  and and_269 (and_269_out, bit_extender_1_out[15], bit_extender_2_out[11]);
  and and_270 (and_270_out, bit_extender_1_out[13], bit_extender_2_out[13]);
  and and_271 (and_271_out, bit_extender_1_out[12], bit_extender_2_out[14]);
  and and_272 (and_272_out, bit_extender_1_out[11], bit_extender_2_out[15]);
  Adder #(.width(1)) adder_215 (
    .a(and_269_out), .b(adder_214_cout), .out(adder_215_out), .cin(and_268_out), .cout(adder_215_cout));
  Adder #(.width(1)) adder_216 (
    .a(adder_215_out), .b(adder_215_cout), .out(adder_216_out), .cin(and_270_out), .cout(adder_216_cout));
  Adder #(.width(1)) adder_217 (
    .a(adder_216_out), .b(adder_216_cout), .out(adder_217_out), .cin(and_271_out), .cout(adder_217_cout));
  Adder #(.width(1)) adder_218 (
    .a(adder_217_out), .b(adder_217_cout), .out(adder_218_out), .cin(and_272_out), .cout(adder_218_cout));
  and and_273 (out_4[26], adder_218_out, in_3);
  and and_274 (and_274_out, bit_extender_1_out[15], bit_extender_2_out[12]);
  and and_275 (and_275_out, bit_extender_1_out[13], bit_extender_2_out[14]);
  and and_276 (and_276_out, bit_extender_1_out[14], bit_extender_2_out[13]);
  and and_277 (and_277_out, bit_extender_1_out[12], bit_extender_2_out[15]);
  Adder #(.width(1)) adder_219 (
    .a(and_274_out), .b(adder_218_cout), .out(adder_219_out), .cin(and_276_out), .cout(adder_219_cout));
  Adder #(.width(1)) adder_220 (
    .a(adder_219_out), .b(adder_219_cout), .out(adder_220_out), .cin(and_275_out), .cout(adder_220_cout));
  and and_278 (and_278_out, bit_extender_1_out[15], bit_extender_2_out[13]);
  Adder #(.width(1)) adder_221 (
    .a(adder_220_out), .b(adder_220_cout), .out(adder_221_out), .cin(and_277_out), .cout(adder_221_cout));
  and and_279 (out_4[27], adder_221_out, in_3);
  and and_280 (and_280_out, bit_extender_1_out[14], bit_extender_2_out[14]);
  and and_281 (and_281_out, bit_extender_1_out[13], bit_extender_2_out[15]);
  Adder #(.width(1)) adder_222 (
    .a(and_278_out), .b(adder_221_cout), .out(adder_222_out), .cin(and_280_out), .cout(adder_222_cout));
  Adder #(.width(1)) adder_223 (
    .a(adder_222_out), .b(adder_222_cout), .out(adder_223_out), .cin(and_281_out), .cout(adder_223_cout));
  and and_282 (out_4[28], adder_223_out, in_3);
  and and_283 (and_283_out, bit_extender_1_out[15], bit_extender_2_out[14]);
  and and_284 (and_284_out, bit_extender_1_out[14], bit_extender_2_out[15]);
  Adder #(.width(1)) adder_224 (
    .a(and_283_out), .b(adder_223_cout), .out(adder_224_out), .cin(and_284_out), .cout(adder_224_cout));
  and and_285 (out_4[29], adder_224_out, in_3);
  and and_286 (and_286_out, bit_extender_1_out[15], bit_extender_2_out[15]);
  and and_287 (out_4[30], somador_2bits_2_resultado, in_3);
  somador_2bits somador_2bits_2 (
    .A(and_286_out), .B(adder_224_cout), .RESULTADO(somador_2bits_2_resultado), .VAI_1(somador_2bits_2_vai_1));
  and and_288 (out_4[31], in_3, somador_2bits_2_vai_1);
endmodule

module somador_2bits (
  input  A,
  input  B,
  output VAI_1,
  output RESULTADO
);

  xor xor_1 (RESULTADO, A, B);
  and and_1 (VAI_1, A, B);
endmodule

module ENABLE (
  input  U1,
  input  U2,
  input  U3,
  input  U4,
  output ENABLE
);

  wire and_1_out, and_3_out, not_1_out, not_2_out, not_3_out;

  not not_1 (not_1_out, U1);
  not not_2 (not_2_out, U2);
  not not_3 (not_3_out, U4);
  and and_1 (and_1_out, not_1_out, not_2_out);
  and and_2 (ENABLE, and_1_out, and_3_out);
  and and_3 (and_3_out, U3, not_3_out);
endmodule
