// Logisim project processador_monociclo_grupo02.circ as structural Verilog: 8 circuits, main circuit main
module main (
  input  Ativa_interface,
  input  Enable,
  input  [31:0] Endereco_mem__inf__pelo_usu,
  input  [4:0] Enrtada_End_Mem
);

  wire controle_1_atuapc, controle_1_clock, controle_1_escrevemem, controle_1_escrevereg, controle_1_lemem,
       controle_1_memparareg, controle_1_origalu, controle_1_regdst, not_1_out, not_2_out, not_3_out,
       or_1_out, or_2_out, or_3_out;
  wire [1:0] controle_1_opalu, controle_alu_1_out_3;
  wire [4:0] \contador_de_programa_1_instrução__11_15 , \contador_de_programa_1_instrução__20_16 ,
       \contador_de_programa_1_instrução__25_21 , multiplexer_1_out, multiplexer_2_out;
  wire [5:0] \contador_de_programa_1_instrução__31_26 , \extensão_de_sinal_1_instrução__5__0 ;
  wire [15:0] \contador_de_programa_1_instrução__0_15 ;
  wire [31:0] alu_32_bits_1_result, banco_de_registradores_1_dados_de_leitura_1,
       banco_de_registradores_1_dados_de_leitura_2, demultiplexer_1_out0, demultiplexer_1_out1,
       \extensão_de_sinal_1_resultado_extens__sinal , memoria_1_output__retorna_ao_b__reg, multiplexer_3_out,
       multiplexer_4_out, multiplexer_5_out, multiplexer_6_out;

  Contador_de_Programa contador_de_programa_1 (
    .AtuaPC(controle_1_atuapc), .\Instrução__0_15 (\contador_de_programa_1_instrução__0_15 ),
    .\Instrução__11_15 (\contador_de_programa_1_instrução__11_15 ),
    .\Instrução__20_16 (\contador_de_programa_1_instrução__20_16 ),
    .\Instrução__25_21 (\contador_de_programa_1_instrução__25_21 ),
    .\Instrução__31_26 (\contador_de_programa_1_instrução__31_26 ));
  Multiplexer #(.width(5)) multiplexer_1 (
    .in0(\contador_de_programa_1_instrução__20_16 ), .in1(\contador_de_programa_1_instrução__11_15 ),
    .out(multiplexer_1_out), .sel(controle_1_regdst));  // open: en
  not not_1 (not_1_out, Ativa_interface);
  Multiplexer #(.width(5)) multiplexer_2 (
    .in0(Enrtada_End_Mem), .in1(\contador_de_programa_1_instrução__25_21 ), .out(multiplexer_2_out),
    .sel(not_1_out));  // open: en
  Controle controle_1 (
    .\Instrução_31_26 (\contador_de_programa_1_instrução__31_26 ), .AtuaPC(controle_1_atuapc),
    .OrigALU(controle_1_origalu), .EscreveMem(controle_1_escrevemem), .LeMem(controle_1_lemem),
    .MemParaReg(controle_1_memparareg), .RegDst(controle_1_regdst), .EscreveReg(controle_1_escrevereg),
    .OpAlu(controle_1_opalu), .Enable(Enable), .Clock(controle_1_clock));
  or or_1 (or_1_out, controle_1_clock, Ativa_interface);
  \Extensão_de_sinal  \extensão_de_sinal_1  (
    .\instrução_15_0 (\contador_de_programa_1_instrução__0_15 ),
    .Resultado_extens__sinal(\extensão_de_sinal_1_resultado_extens__sinal ),
    .\Instrução__5__0 (\extensão_de_sinal_1_instrução__5__0 ));
  Banco_de_Registradores banco_de_registradores_1 (
    .Clock(or_1_out), .Registrador_de_leitura_1(multiplexer_2_out),
    .Registrador_de_leitura_2(\contador_de_programa_1_instrução__20_16 ),
    .Registrador_para_escrita(multiplexer_1_out),
    .Dados_de_leitura_1(banco_de_registradores_1_dados_de_leitura_1), .Escreve_Reg(controle_1_escrevereg),
    .Dados_de_leitura_2(banco_de_registradores_1_dados_de_leitura_2), .Dados_para_escrita(multiplexer_4_out),
    .Enable(Enable));
  Demultiplexer #(.width(32)) demultiplexer_1 (
    .out0(demultiplexer_1_out0), .out1(demultiplexer_1_out1),
    .in(banco_de_registradores_1_dados_de_leitura_1), .sel(Ativa_interface));  // open: en
  Controle_ALU controle_alu_1 (
    .Instruao_5__0(\extensão_de_sinal_1_instrução__5__0 ), .OpAlu1(controle_1_opalu),
    .out_3(controle_alu_1_out_3));
  Alu_32_bits alu_32_bits_1 (
    .Controle_ALU(controle_alu_1_out_3), .\EXTENSÃO (\extensão_de_sinal_1_resultado_extens__sinal ),
    .Input_ALU_1(demultiplexer_1_out0), .Input_ALU_2(banco_de_registradores_1_dados_de_leitura_2),
    .OrigiAlu(controle_1_origalu), .Cin(1'b0), .RESULT(alu_32_bits_1_result), .Clock(controle_1_clock),
    .Enable(Enable));
  not not_2 (not_2_out, Ativa_interface);
  Multiplexer #(.width(32)) multiplexer_3 (
    .in0(Endereco_mem__inf__pelo_usu), .in1(alu_32_bits_1_result), .out(multiplexer_3_out), .sel(not_2_out));  // open: en
  or or_2 (or_2_out, Ativa_interface, controle_1_lemem);
  or or_3 (or_3_out, Ativa_interface, controle_1_clock);
  Memoria memoria_1 (
    .Resultado_da_ALU(multiplexer_3_out), .Input_de_dados(banco_de_registradores_1_dados_de_leitura_2),
    .Output__retorna_ao_b__reg(memoria_1_output__retorna_ao_b__reg), .LeMem(or_2_out), .Clock(or_3_out),
    .EscreveMem(controle_1_escrevemem), .Enable(Enable));
  not not_3 (not_3_out, controle_1_memparareg);
  Multiplexer #(.width(32)) multiplexer_4 (
    .in0(memoria_1_output__retorna_ao_b__reg), .in1(alu_32_bits_1_result), .out(multiplexer_4_out),
    .sel(not_3_out));  // open: en
  Multiplexer #(.width(32)) multiplexer_5 (
    .in1(memoria_1_output__retorna_ao_b__reg), .out(multiplexer_5_out), .sel(Ativa_interface));  // open: in0, en
  Multiplexer #(.width(32)) multiplexer_6 (
    .in1(demultiplexer_1_out1), .out(multiplexer_6_out), .sel(Ativa_interface));  // open: in0, en
  Hex_Digit_Display hex_digit_display_1 (.value(multiplexer_5_out[27:24]));  // open: dp
  Hex_Digit_Display hex_digit_display_2 (.value(multiplexer_5_out[31:28]));  // open: dp
  Hex_Digit_Display hex_digit_display_3 (.value(multiplexer_6_out[27:24]));  // open: dp
  Hex_Digit_Display hex_digit_display_4 (.value(multiplexer_6_out[31:28]));  // open: dp
  Hex_Digit_Display hex_digit_display_5 (.value(multiplexer_5_out[23:20]));  // open: dp
  Hex_Digit_Display hex_digit_display_6 (.value(multiplexer_6_out[23:20]));  // open: dp
  Hex_Digit_Display hex_digit_display_7 (.value(multiplexer_5_out[19:16]));  // open: dp
  Hex_Digit_Display hex_digit_display_8 (.value(multiplexer_6_out[19:16]));  // open: dp
  Hex_Digit_Display hex_digit_display_9 (.value(multiplexer_5_out[15:12]));  // open: dp
  Hex_Digit_Display hex_digit_display_10 (.value(multiplexer_5_out[11:8]));  // open: dp
  Hex_Digit_Display hex_digit_display_11 (.value(multiplexer_6_out[15:12]));  // open: dp
  Hex_Digit_Display hex_digit_display_12 (.value(multiplexer_6_out[11:8]));  // open: dp
  Hex_Digit_Display hex_digit_display_13 (.value(multiplexer_5_out[7:4]));  // open: dp
  Hex_Digit_Display hex_digit_display_14 (.value(multiplexer_6_out[7:4]));  // open: dp
  Hex_Digit_Display hex_digit_display_15 (.value(multiplexer_5_out[3:0]));  // open: dp
  Hex_Digit_Display hex_digit_display_16 (.value(multiplexer_6_out[3:0]));  // open: dp

  // Notes on the sheet:
  //   Memória de
  //   Instrucões
  //   [31..26]
  //   [25..21]
  //   [20..16]
  //   [15..11]
  //   [15..0]
  //   AtuaPC
  //   RegDst
  //   Clock
  //   EscreveReg
  //   Reg. Leit. 1
  //   Reg. Leit. 2
  //   OrigALU
  //   Controle
  //   LeMem
  //   Enable
  //   Registrador para Escrita
  //   Dados para escrita
  //   [15..0]
  //   EscreveMem
  //   MemParaReg
  //   EscreveReg
  //   Clock
  //   Dados de leitura 1
  //   Banco de
  //   Registradores
  //   Dados de leitura 2
  //   Result. Ext. Sinal
  //   [5..0]
  //   [5..0]
  //   OpALU
  //   Controle
  //   ALU
  //   Input ALU 1
  //   Input ALU 2
  //   Result. Ext
  //   Result. ALU
  //   ALU
  //   LeMem
  //   Endereco
  //   Dados para escrita
  //   Clock
  //   Memória de Dados
  //   Enable
  //   EscreveMem
endmodule

module Banco_de_Registradores (
  input  Clock,
  input  Escreve_Reg,
  input  [4:0] Registrador_de_leitura_1,
  input  [4:0] Registrador_de_leitura_2,
  input  [31:0] Dados_para_escrita,
  input  [4:0] Registrador_para_escrita,
  input  Enable,
  output [31:0] Dados_de_leitura_1,
  output [31:0] Dados_de_leitura_2
);

  wire and_1_out, and_2_out, and_3_out, and_4_out, and_5_out, and_6_out, and_7_out, and_8_out, and_9_out,
       and_10_out, and_11_out, and_12_out, and_13_out, and_14_out, and_15_out, and_16_out, and_17_out,
       and_18_out, and_19_out, and_20_out, and_21_out, and_22_out, and_23_out, and_24_out, and_25_out,
       and_26_out, and_27_out, and_28_out, and_29_out, and_30_out, and_31_out, and_32_out, decoder_1_out0,
       decoder_1_out1, decoder_2_out0, decoder_2_out1, decoder_2_out2, decoder_2_out3, decoder_2_out4,
       decoder_2_out5, decoder_2_out6, decoder_2_out7, decoder_2_out8, decoder_2_out9, decoder_2_out10,
       decoder_2_out11, decoder_2_out12, decoder_2_out13, decoder_2_out14, decoder_2_out15, decoder_2_out16,
       decoder_2_out17, decoder_2_out18, decoder_2_out19, decoder_2_out20, decoder_2_out21, decoder_2_out22,
       decoder_2_out23, decoder_2_out24, decoder_2_out25, decoder_2_out26, decoder_2_out27, decoder_2_out28,
       decoder_2_out29, decoder_2_out30, decoder_2_out31, not_1_out;
  wire [31:0] register_1_q, register_2_q, register_3_q, register_4_q, register_5_q, register_6_q,
       register_7_q, register_8_q, register_9_q, register_10_q, register_11_q, register_12_q, register_13_q,
       register_14_q, register_15_q, register_16_q, register_17_q, register_18_q, register_19_q,
       register_20_q, register_21_q, register_22_q, register_23_q, register_24_q, register_25_q,
       register_26_q, register_27_q, register_28_q, register_29_q, register_30_q, register_31_q,
       register_32_q;

  Decoder decoder_1 (.out0(decoder_1_out0), .out1(decoder_1_out1), .sel(Escreve_Reg));  // open: en
  not not_1 (not_1_out, Enable);
  Decoder #(.select(5)) decoder_2 (
    .out0(decoder_2_out0), .out1(decoder_2_out1), .out2(decoder_2_out2), .out3(decoder_2_out3),
    .out4(decoder_2_out4), .out5(decoder_2_out5), .out6(decoder_2_out6), .out7(decoder_2_out7),
    .out8(decoder_2_out8), .out9(decoder_2_out9), .out10(decoder_2_out10), .out11(decoder_2_out11),
    .out12(decoder_2_out12), .out13(decoder_2_out13), .out14(decoder_2_out14), .out15(decoder_2_out15),
    .out16(decoder_2_out16), .out17(decoder_2_out17), .out18(decoder_2_out18), .out19(decoder_2_out19),
    .out20(decoder_2_out20), .out21(decoder_2_out21), .out22(decoder_2_out22), .out23(decoder_2_out23),
    .out24(decoder_2_out24), .out25(decoder_2_out25), .out26(decoder_2_out26), .out27(decoder_2_out27),
    .out28(decoder_2_out28), .out29(decoder_2_out29), .out30(decoder_2_out30), .out31(decoder_2_out31),
    .sel(Registrador_para_escrita));  // open: en
  Register #(.width(32), .trigger("falling")) register_1 (
    .D(Dados_para_escrita), .en(and_1_out), .Q(register_1_q), .clk(Clock), .clr(not_1_out));
  and and_1 (and_1_out, decoder_2_out0, decoder_1_out1);
  Register #(.width(32), .trigger("falling")) register_2 (
    .D(Dados_para_escrita), .en(and_2_out), .Q(register_2_q), .clk(Clock), .clr(not_1_out));
  and and_2 (and_2_out, decoder_2_out4, decoder_1_out1);
  Register #(.width(32), .trigger("falling")) register_3 (
    .D(Dados_para_escrita), .en(and_3_out), .Q(register_3_q), .clk(Clock), .clr(not_1_out));
  and and_3 (and_3_out, decoder_2_out8, decoder_1_out1);
  Register #(.width(32), .trigger("falling")) register_4 (
    .D(Dados_para_escrita), .en(and_4_out), .Q(register_4_q), .clk(Clock), .clr(not_1_out));
  and and_4 (and_4_out, decoder_2_out12, decoder_1_out1);
  Register #(.width(32), .trigger("falling")) register_5 (
    .D(Dados_para_escrita), .en(and_5_out), .Q(register_5_q), .clk(Clock), .clr(not_1_out));
  and and_5 (and_5_out, decoder_2_out16, decoder_1_out1);
  Register #(.width(32), .trigger("falling")) register_6 (
    .D(Dados_para_escrita), .en(and_6_out), .Q(register_6_q), .clk(Clock), .clr(not_1_out));
  and and_6 (and_6_out, decoder_2_out20, decoder_1_out1);
  and and_7 (and_7_out, decoder_2_out24, decoder_1_out1);
  and and_8 (and_8_out, decoder_2_out28, decoder_1_out1);
  Register #(.width(32), .trigger("falling")) register_7 (
    .D(Dados_para_escrita), .en(and_7_out), .Q(register_7_q), .clk(Clock), .clr(not_1_out));
  Register #(.width(32), .trigger("falling")) register_8 (
    .D(Dados_para_escrita), .en(and_8_out), .Q(register_8_q), .clk(Clock), .clr(not_1_out));
  Register #(.width(32), .trigger("falling")) register_9 (
    .D(Dados_para_escrita), .en(and_9_out), .Q(register_9_q), .clk(Clock), .clr(not_1_out));
  and and_9 (and_9_out, decoder_2_out1, decoder_1_out1);
  Register #(.width(32), .trigger("falling")) register_10 (
    .D(Dados_para_escrita), .en(and_10_out), .Q(register_10_q), .clk(Clock), .clr(not_1_out));
  and and_10 (and_10_out, decoder_2_out5, decoder_1_out1);
  Register #(.width(32), .trigger("falling")) register_11 (
    .D(Dados_para_escrita), .en(and_11_out), .Q(register_11_q), .clk(Clock), .clr(not_1_out));
  and and_11 (and_11_out, decoder_2_out9, decoder_1_out1);
  Register #(.width(32), .trigger("falling")) register_12 (
    .D(Dados_para_escrita), .en(and_12_out), .Q(register_12_q), .clk(Clock), .clr(not_1_out));
  and and_12 (and_12_out, decoder_2_out13, decoder_1_out1);
  Register #(.width(32), .trigger("falling")) register_13 (
    .D(Dados_para_escrita), .en(and_13_out), .Q(register_13_q), .clk(Clock), .clr(not_1_out));
  and and_13 (and_13_out, decoder_2_out17, decoder_1_out1);
  Register #(.width(32), .trigger("falling")) register_14 (
    .D(Dados_para_escrita), .en(and_14_out), .Q(register_14_q), .clk(Clock), .clr(not_1_out));
  and and_14 (and_14_out, decoder_2_out21, decoder_1_out1);
  and and_15 (and_15_out, decoder_2_out25, decoder_1_out1);
  and and_16 (and_16_out, decoder_2_out29, decoder_1_out1);
  Register #(.width(32), .trigger("falling")) register_15 (
    .D(Dados_para_escrita), .en(and_15_out), .Q(register_15_q), .clk(Clock), .clr(not_1_out));
  Register #(.width(32), .trigger("falling")) register_16 (
    .D(Dados_para_escrita), .en(and_16_out), .Q(register_16_q), .clk(Clock), .clr(not_1_out));
  Register #(.width(32), .trigger("falling")) register_17 (
    .D(Dados_para_escrita), .en(and_17_out), .Q(register_17_q), .clk(Clock), .clr(not_1_out));
  and and_17 (and_17_out, decoder_2_out2, decoder_1_out1);
  Register #(.width(32), .trigger("falling")) register_18 (
    .D(Dados_para_escrita), .en(and_18_out), .Q(register_18_q), .clk(Clock), .clr(not_1_out));
  and and_18 (and_18_out, decoder_2_out6, decoder_1_out1);
  Register #(.width(32), .trigger("falling")) register_19 (
    .D(Dados_para_escrita), .en(and_19_out), .Q(register_19_q), .clk(Clock), .clr(not_1_out));
  and and_19 (and_19_out, decoder_2_out10, decoder_1_out1);
  Register #(.width(32), .trigger("falling")) register_20 (
    .D(Dados_para_escrita), .en(and_20_out), .Q(register_20_q), .clk(Clock), .clr(not_1_out));
  and and_20 (and_20_out, decoder_2_out14, decoder_1_out1);
  Register #(.width(32), .trigger("falling")) register_21 (
    .D(Dados_para_escrita), .en(and_21_out), .Q(register_21_q), .clk(Clock), .clr(not_1_out));
  and and_21 (and_21_out, decoder_2_out18, decoder_1_out1);
  Register #(.width(32), .trigger("falling")) register_22 (
    .D(Dados_para_escrita), .en(and_22_out), .Q(register_22_q), .clk(Clock), .clr(not_1_out));
  and and_22 (and_22_out, decoder_2_out22, decoder_1_out1);
  Register #(.width(32), .trigger("falling")) register_23 (
    .D(Dados_para_escrita), .en(and_23_out), .Q(register_23_q), .clk(Clock), .clr(not_1_out));
  and and_23 (and_23_out, decoder_2_out26, decoder_1_out1);
  Register #(.width(32), .trigger("falling")) register_24 (
    .D(Dados_para_escrita), .en(and_24_out), .Q(register_24_q), .clk(Clock), .clr(not_1_out));
  and and_24 (and_24_out, decoder_2_out30, decoder_1_out1);
  and and_25 (and_25_out, decoder_2_out7, decoder_1_out1);
  and and_26 (and_26_out, decoder_2_out11, decoder_1_out1);
  and and_27 (and_27_out, decoder_2_out15, decoder_1_out1);
  and and_28 (and_28_out, decoder_2_out19, decoder_1_out1);
  and and_29 (and_29_out, decoder_2_out23, decoder_1_out1);
  and and_30 (and_30_out, decoder_2_out31, decoder_1_out1);
  Register #(.width(32), .trigger("falling")) register_25 (
    .D(Dados_para_escrita), .en(and_31_out), .Q(register_25_q), .clk(Clock), .clr(not_1_out));
  and and_31 (and_31_out, decoder_2_out3, decoder_1_out1);
  Register #(.width(32), .trigger("falling")) register_26 (
    .D(Dados_para_escrita), .en(and_25_out), .Q(register_26_q), .clk(Clock), .clr(not_1_out));
  Register #(.width(32), .trigger("falling")) register_27 (
    .D(Dados_para_escrita), .en(and_26_out), .Q(register_27_q), .clk(Clock), .clr(not_1_out));
  Register #(.width(32), .trigger("falling")) register_28 (
    .D(Dados_para_escrita), .en(and_27_out), .Q(register_28_q), .clk(Clock), .clr(not_1_out));
  Register #(.width(32), .trigger("falling")) register_29 (
    .D(Dados_para_escrita), .en(and_28_out), .Q(register_29_q), .clk(Clock), .clr(not_1_out));
  Register #(.width(32), .trigger("falling")) register_30 (
    .D(Dados_para_escrita), .en(and_29_out), .Q(register_30_q), .clk(Clock), .clr(not_1_out));
  Register #(.width(32), .trigger("falling")) register_31 (
    .D(Dados_para_escrita), .en(and_32_out), .Q(register_31_q), .clk(Clock), .clr(not_1_out));
  and and_32 (and_32_out, decoder_2_out27, decoder_1_out1);
  Register #(.width(32), .trigger("falling")) register_32 (
    .D(Dados_para_escrita), .en(and_30_out), .Q(register_32_q), .clk(Clock), .clr(not_1_out));
  Multiplexer #(.select(5), .width(32)) multiplexer_1 (
    .in0(register_1_q), .in1(register_9_q), .in2(register_17_q), .in3(register_25_q), .in4(register_2_q),
    .in5(register_10_q), .in6(register_18_q), .in7(register_26_q), .in8(register_3_q), .in9(register_11_q),
    .in10(register_19_q), .in11(register_27_q), .in12(register_4_q), .in13(register_12_q),
    .in14(register_20_q), .in15(register_28_q), .in16(register_5_q), .in17(register_13_q),
    .in18(register_21_q), .in19(register_29_q), .in20(register_6_q), .in21(register_14_q),
    .in22(register_22_q), .in23(register_30_q), .in24(register_7_q), .in25(register_15_q),
    .in26(register_23_q), .in27(register_31_q), .in28(register_8_q), .in29(register_16_q),
    .in30(register_24_q), .in31(register_32_q), .out(Dados_de_leitura_2), .sel(Registrador_de_leitura_2),
    .en(decoder_1_out0));
  Multiplexer #(.select(5), .width(32)) multiplexer_2 (
    .in0(register_1_q), .in1(register_9_q), .in2(register_17_q), .in3(register_25_q), .in4(register_2_q),
    .in5(register_10_q), .in6(register_18_q), .in7(register_26_q), .in8(register_3_q), .in9(register_11_q),
    .in10(register_19_q), .in11(register_27_q), .in12(register_4_q), .in13(register_12_q),
    .in14(register_20_q), .in15(register_28_q), .in16(register_5_q), .in17(register_13_q),
    .in18(register_21_q), .in19(register_29_q), .in20(register_6_q), .in21(register_14_q),
    .in22(register_22_q), .in23(register_30_q), .in24(register_7_q), .in25(register_15_q),
    .in26(register_23_q), .in27(register_31_q), .in28(register_8_q), .in29(register_16_q),
    .in30(register_24_q), .in31(register_32_q), .out(Dados_de_leitura_1), .sel(Registrador_de_leitura_1),
    .en(decoder_1_out0));
endmodule

module Memoria (
  input  LeMem,
  input  Clock,
  input  EscreveMem,
  input  [31:0] Resultado_da_ALU,
  input  [31:0] Input_de_dados,
  input  Enable,
  output [31:0] Output__retorna_ao_b__reg
);

  wire multiplexer_1_out, not_1_out, not_2_out, or_1_out;

  not not_1 (not_1_out, Clock);
  Multiplexer multiplexer_1 (.in0(Clock), .in1(not_1_out), .out(multiplexer_1_out), .sel(EscreveMem));  // open: en
  or or_1 (or_1_out, EscreveMem, LeMem);
  not not_2 (not_2_out, Enable);
  RAM #(.addrWidth(24), .dataWidth(32), .bus("separate")) ram_1 (
    .addr(Resultado_da_ALU[23:0]), .din(Input_de_dados), .data(Output__retorna_ao_b__reg), .str(EscreveMem),
    .sel(or_1_out), .clk(multiplexer_1_out), .ld(LeMem), .clr(not_2_out));
  // also tied to GND on the sheet: {Resultado_da_ALU[24], Resultado_da_ALU[25], Resultado_da_ALU[26], Resultado_da_ALU[27], Resultado_da_ALU[28], Resultado_da_ALU[29], Resultado_da_ALU[30], Resultado_da_ALU[31]}
endmodule

module Alu_32_bits (
  input  OrigiAlu,
  input  Cin,
  input  [1:0] Controle_ALU,
  input  Clock,
  input  [31:0] Input_ALU_1,
  input  [31:0] Input_ALU_2,
  input  [31:0] \EXTENSÃO ,
  input  Enable,
  output [31:0] RESULT
);

  wire and_1_out, not_1_out, not_2_out;
  wire [1:0] counter_1_q;
  wire [31:0] adder_1_out, main_1_out_4, multiplexer_1_out, multiplexer_2_out, multiplicador_32_bits_1_out_4,
       subtractor_1_out;

  Multiplexer #(.width(32), .enable("false")) multiplexer_1 (
    .in0(Input_ALU_2), .in1(\EXTENSÃO ), .out(multiplexer_1_out), .sel(OrigiAlu));
  \CircuitoDivisorVersãoFinal2_main  main_1 (
    .Bit_Enable(Enable), .in_1(Input_ALU_1), .in_2(multiplexer_1_out), .out_4(main_1_out_4));  // open: out_5
  Subtractor #(.width(32)) subtractor_1 (
    .a(Input_ALU_1), .b(multiplexer_1_out), .out(subtractor_1_out), .bin(Cin));  // open: bout
  MULTIPLICADOR_32_BITS multiplicador_32_bits_1 (
    .in_1(Input_ALU_1), .in_2(multiplexer_1_out), .out_4(multiplicador_32_bits_1_out_4), .in_3(Enable));
  Adder #(.width(32)) adder_1 (.a(Input_ALU_1), .b(multiplexer_1_out), .out(adder_1_out), .cin(Cin));  // open: cout
  Multiplexer #(.select(2), .width(32), .enable("false")) multiplexer_2 (
    .in0(adder_1_out), .in1(subtractor_1_out), .in2(multiplicador_32_bits_1_out_4), .in3(main_1_out_4),
    .out(multiplexer_2_out), .sel(Controle_ALU));
  Counter #(.width(2), .max('h3)) counter_1 (
    .Q(counter_1_q), .clk(Clock), .clr(not_1_out));  // open: load, D, count, carry
  not not_1 (not_1_out, Enable);
  not not_2 (not_2_out, and_1_out);
  and and_1 (and_1_out, counter_1_q[0], ~counter_1_q[1]);  // AND_Gate
  RAM #(.addrWidth(2), .dataWidth(32), .bus("separate")) ram_1 (
    .addr(2'b00), .din(multiplexer_2_out), .data(RESULT), .str(and_1_out), .sel(Clock), .clk(Clock),
    .ld(not_2_out));  // open: clr

  // Notes on the sheet:
  //   Divisor
  //   Multiplicador
  //   00 - Soma
  //   01 - Subtração
  //   10 - Multiplicação
  //   11 - Divisão
endmodule

module Controle_ALU (
  input  [1:0] OpAlu1,
  input  [5:0] Instruao_5__0,
  output [1:0] out_3
);

  wire and_1_out, and_2_out, and_3_out, and_4_out, and_5_out, not_1_out, not_2_out, not_3_out, OP0_out,
       OP1_out, OP2_out, OP3_out, or_1_out;

  or or_1 (or_1_out, Instruao_5__0[3], Instruao_5__0[0]);
  not not_1 (not_1_out, OpAlu1[0]);
  and and_1 (and_1_out, OpAlu1[1], Instruao_5__0[1]);
  not not_2 (not_2_out, Instruao_5__0[2]);
  not not_3 (not_3_out, OpAlu1[1]);
  and OP0 (OP0_out, OpAlu1[1], or_1_out);
  and OP3 (OP3_out, OpAlu1[0], not_1_out);
  or OP2 (OP2_out, OpAlu1[0], and_1_out);
  or OP1 (OP1_out, not_2_out, not_3_out);
  and and_2 (and_2_out, OP2_out, ~OP1_out, OP0_out);  // AND_Gate
  and and_3 (and_3_out, OP2_out, OP1_out, ~OP0_out);  // AND_Gate
  and and_4 (and_4_out, ~OP2_out, OP1_out, OP0_out);  // AND_Gate
  and and_5 (and_5_out, OP2_out, OP1_out, OP0_out);
  or or_2 (out_3[0], and_3_out, and_2_out, and_5_out);
  or or_3 (out_3[1], and_4_out, and_2_out, and_5_out);

  assign Instruao_5__0[4] = Instruao_5__0[5];
  // also tied to GND on the sheet: {OP3_out, Instruao_5__0[5]}

  // Notes on the sheet:
  //   00 - Soma
  //   01 - Subtração
  //   10 - Multiplicação
  //   11 - Divisão
endmodule

// Ext. Sinal
module \Extensão_de_sinal  (
  input  [15:0] \instrução_15_0 ,
  output [31:0] Resultado_extens__sinal,
  output [5:0] \Instrução__5__0 
);

  assign Resultado_extens__sinal = {{16{1'b0}}, \instrução_15_0 };  // Bit_Extender bit_extender_1
  Bit_Extender #(.in_width(16), .out_width(6)) bit_extender_2 (.in(\instrução_15_0 ), .out(\Instrução__5__0 ));
endmodule

module Contador_de_Programa (
  input  AtuaPC,
  output [15:0] \Instrução__0_15 ,
  output [4:0] \Instrução__11_15 ,
  output [4:0] \Instrução__20_16 ,
  output [4:0] \Instrução__25_21 ,
  output [5:0] \Instrução__31_26 
);

  wire button_1_out, not_1_out;
  wire [23:0] bitselector_1_out;
  wire [31:0] adder_1_out, register_1_q;

  Button button_1 (.out(button_1_out));
  Adder #(.width(32)) adder_1 (.a(register_1_q), .b(32'h1), .out(adder_1_out));  // open: cin, cout
  Register #(.width(32)) register_1 (.D(adder_1_out), .Q(register_1_q), .clk(AtuaPC), .clr(button_1_out));  // open: en
  Controlled_Buffer #(.width(32)) controlled_buffer_1 (
    .out({\Instrução__31_26 , \Instrução__25_21 , \Instrução__20_16 , \Instrução__0_15 }), .en(1'b0));  // open: in
  BitSelector #(.width(32), .group(24)) bitselector_1 (.in(register_1_q), .out(bitselector_1_out), .sel(1'b0));
  not not_1 (not_1_out, 1'b0);
  RAM #(.addrWidth(24), .dataWidth(32)) ram_1 (
    .addr(bitselector_1_out),
    .data({\Instrução__31_26 , \Instrução__25_21 , \Instrução__20_16 , \Instrução__0_15 }), .clk(AtuaPC),
    .ld(not_1_out), .clr(button_1_out));  // open: sel

  assign \Instrução__11_15  = \Instrução__0_15 [15:11];

  // Notes on the sheet:
  //   Reset
endmodule

module Controle (
  input  [5:0] \Instrução_31_26 ,
  input  Enable,
  output AtuaPC,
  output [1:0] OpAlu,
  output OrigALU,
  output EscreveMem,
  output LeMem,
  output MemParaReg,
  output Clock,
  output RegDst,
  output EscreveReg
);

  wire and_1_out, and_4_out, and_5_out, and_6_out, and_7_out, and_8_out, and_9_out, and_14_out, and_15_out,
       clock_1_out, not_1_out, not_2_out, not_3_out, not_4_out, not_5_out, not_6_out, not_7_out, not_8_out,
       not_9_out, not_10_out, not_11_out, not_12_out, not_13_out, not_14_out, not_15_out, not_16_out,
       not_17_out, not_18_out;
  wire [1:0] counter_1_q;

  and and_1 (and_1_out, \Instrução_31_26 [5], \Instrução_31_26 [4], \Instrução_31_26 [3], \Instrução_31_26 [2], \Instrução_31_26 [1], \Instrução_31_26 [0]);
  not not_1 (not_1_out, and_1_out);
  Clock clock_1 (.out(clock_1_out));
  Counter #(.width(2), .max('h3)) counter_1 (
    .Q(counter_1_q), .clk(Clock), .clr(not_2_out));  // open: load, D, count, carry
  and and_2 (Clock, not_1_out, clock_1_out, Enable);
  not not_2 (not_2_out, Enable);
  not not_3 (not_3_out, \Instrução_31_26 [4]);
  not not_4 (not_4_out, counter_1_q[1]);
  not not_5 (not_5_out, counter_1_q[0]);
  not not_6 (not_6_out, \Instrução_31_26 [0]);
  not not_7 (not_7_out, \Instrução_31_26 [0]);
  not not_8 (not_8_out, \Instrução_31_26 [5]);
  not not_9 (not_9_out, \Instrução_31_26 [4]);
  not not_10 (not_10_out, \Instrução_31_26 [2]);
  not not_11 (not_11_out, \Instrução_31_26 [2]);
  not not_12 (not_12_out, \Instrução_31_26 [4]);
  not not_13 (not_13_out, counter_1_q[0]);
  not not_14 (not_14_out, \Instrução_31_26 [3]);
  not not_15 (not_15_out, \Instrução_31_26 [3]);
  not not_16 (not_16_out, \Instrução_31_26 [0]);
  not not_17 (not_17_out, \Instrução_31_26 [3]);
  not not_18 (not_18_out, \Instrução_31_26 [1]);
  and and_3 (AtuaPC, not_3_out, not_4_out, not_5_out);
  and and_4 (and_4_out, \Instrução_31_26 [5], not_6_out, counter_1_q[0]);
  and and_5 (and_5_out, \Instrução_31_26 [5], not_7_out, counter_1_q[1]);
  and and_6 (and_6_out, not_8_out, counter_1_q[0]);
  and and_7 (and_7_out, not_9_out, \Instrução_31_26 [0], counter_1_q[0]);
  and and_8 (and_8_out, not_10_out, \Instrução_31_26 [0], counter_1_q[1]);
  and and_9 (and_9_out, \Instrução_31_26 [3], not_11_out, counter_1_q[1]);
  and and_10 (EscreveMem, not_12_out, \Instrução_31_26 [3], \Instrução_31_26 [0], counter_1_q[1], not_13_out);
  and and_11 (LeMem, not_14_out, \Instrução_31_26 [0], counter_1_q[1], counter_1_q[0]);
  and and_12 (MemParaReg, not_15_out, \Instrução_31_26 [0], counter_1_q[1], counter_1_q[0]);
  and and_13 (RegDst, \Instrução_31_26 [5], not_16_out, counter_1_q[1], counter_1_q[0]);
  and and_14 (and_14_out, not_17_out, counter_1_q[1], counter_1_q[0]);
  and and_15 (and_15_out, not_18_out, counter_1_q[1], counter_1_q[0]);
  or or_1 (OpAlu[1], and_4_out, and_5_out);
  or or_2 (OrigALU, and_6_out, and_7_out, and_8_out, and_9_out);
  or or_3 (EscreveReg, and_14_out, and_15_out);

  assign OpAlu[0] = 1'b0;

  // Notes on the sheet:
  //   Clock: pull=up
endmodule
